// Logisim project Projet.circ as structural Verilog
module main (
  input  CHA,
  input  CHB,
  input  CHC,
  input  Reset,
  input  Stop_Alarm,
  input  Actiavte_Alarm,
  input  Set,
  input  Start,
  input  Switch_Mode,
  output [47:0] Display,
  output LED_0,
  output LED_1,
  output LED_2,
  output LED_3,
  output LED_4,
  output LED_5,
  output LED_6,
  output LED_7,
  output LED_8,
  output LED_9,
  output Buzzer_Output
);

  wire demultiplexer_2_out2, demultiplexer_2_out6, demultiplexer_2_out8, demultiplexer_3_out2,
       demultiplexer_3_out6, demultiplexer_3_out8, demultiplexer_4_out2, demultiplexer_4_out6,
       demultiplexer_4_out8, demultiplexer_5_out2, demultiplexer_5_out4, demultiplexer_5_out6,
       demultiplexer_5_out8, demultiplexer_6_out4, demultiplexer_6_out6, Encodeur_FSM_1_g5,
       Encodeur_FSM_1_updown, Fifth_Sec_Clock_out, Init_Impulse_1_reset, Message_ALARM_1_message_done,
       Message_CHRONO_1_message_done, Message_HELLO_1_message_done, Message_TIME_1_message_done,
       Message_TIMER_1_message_done, Mode_03_Timer_1_buzzer_output, Mode_04_Alarm_1_buzzer, not_1_out,
       or_1_out, xor_1_out;
  wire [1:0] demultiplexer_1_out0, demultiplexer_1_out1, demultiplexer_1_out3, demultiplexer_1_out5,
       demultiplexer_1_out7, Mode_01_Time_1_counting, Mode_02_Chrono_1_counting, Mode_03_Timer_1_counting,
       Mode_FSM_1_start;
  wire [3:0] Mode_FSM_1_mode;
  wire [4:0] d_ff_5_q;
  wire [5:0] Mode_01_Time_1_current_hour, Mode_01_Time_1_current_minute, Mode_01_Time_1_current_second;
  wire [7:0] Mode_01_Time_1_hour_1, Mode_01_Time_1_hour_10, Mode_01_Time_1_min_1, Mode_01_Time_1_min_10,
       Mode_01_Time_1_sec_1, Mode_01_Time_1_sec_10, Mode_02_Chrono_1_hour_1, Mode_02_Chrono_1_hour_10,
       Mode_02_Chrono_1_min_1, Mode_02_Chrono_1_min_10, Mode_02_Chrono_1_sec_1, Mode_02_Chrono_1_sec_10,
       Mode_03_Timer_1_hour_1, Mode_03_Timer_1_hour_10, Mode_03_Timer_1_min_1, Mode_03_Timer_1_min_10,
       Mode_03_Timer_1_sec_1, Mode_03_Timer_1_sec_10, Mode_04_Alarm_1_hour_1, Mode_04_Alarm_1_hour_10,
       Mode_04_Alarm_1_min_1, Mode_04_Alarm_1_min_10, Mode_04_Alarm_1_sec_1, Mode_04_Alarm_1_sec_10;
  wire [9:0] LtR_FSM_1_leds, LtR_FSM_2_leds, RtL_FSM_1_leds;
  wire [47:0] Message_ALARM_1_output_to_display, Message_CHRONO_1_output_to_display,
       Message_HELLO_1_output_to_display, Message_TIME_1_output_to_display, Message_TIMER_1_output_to_display;

  or or_1 (or_1_out, d_ff_5_q[4], d_ff_5_q[3], d_ff_5_q[2], d_ff_5_q[1], d_ff_5_q[0]);
  Init_Impulse Init_Impulse_1 (.Reset(Init_Impulse_1_reset));
  Demultiplexer #(.enable("true"), .select(4), .width(2)) demultiplexer_1 (
    .out0(demultiplexer_1_out0), .out1(demultiplexer_1_out1), .out3(demultiplexer_1_out3),
    .out5(demultiplexer_1_out5), .out7(demultiplexer_1_out7), .in(Mode_FSM_1_start), .sel(Mode_FSM_1_mode),
    .en(1'b1));  // open: out2, out4, out6, out8, out9, out10, out11, out12, out13, out14, out15
  Mode_FSM Mode_FSM_1 (
    .Message_Done(or_1_out), .Switch_Button(Switch_Mode), .Reset_General(Reset), .Mode(Mode_FSM_1_mode),
    .Start(Mode_FSM_1_start[0]), .Reset(Mode_FSM_1_start[1]));
  Demultiplexer #(.enable("true"), .select(4)) demultiplexer_2 (
    .out2(demultiplexer_2_out2), .out6(demultiplexer_2_out6), .out8(demultiplexer_2_out8),
    .in(Encodeur_FSM_1_updown), .sel(Mode_FSM_1_mode), .en(1'b1));  // open: out0, out1, out3, out4, out5, out7, out9, out10, out11, out12, out13, out14, out15
  Encodeur_FSM Encodeur_FSM_1 (.UpDown(Encodeur_FSM_1_updown), .G5(Encodeur_FSM_1_g5), .CHA(CHA), .CHB(CHB));
  Demultiplexer #(.enable("true"), .select(4)) demultiplexer_3 (
    .out2(demultiplexer_3_out2), .out6(demultiplexer_3_out6), .out8(demultiplexer_3_out8),
    .in(Encodeur_FSM_1_g5), .sel(Mode_FSM_1_mode), .en(1'b1));  // open: out0, out1, out3, out4, out5, out7, out9, out10, out11, out12, out13, out14, out15
  not not_1 (not_1_out, CHC);
  Demultiplexer #(.enable("true"), .select(4)) demultiplexer_4 (
    .out2(demultiplexer_4_out2), .out6(demultiplexer_4_out6), .out8(demultiplexer_4_out8), .in(not_1_out),
    .sel(Mode_FSM_1_mode), .en(1'b1));  // open: out0, out1, out3, out4, out5, out7, out9, out10, out11, out12, out13, out14, out15
  Demultiplexer #(.enable("true"), .select(4)) demultiplexer_5 (
    .out2(demultiplexer_5_out2), .out4(demultiplexer_5_out4), .out6(demultiplexer_5_out6),
    .out8(demultiplexer_5_out8), .in(Set), .sel(Mode_FSM_1_mode), .en(1'b1));  // open: out0, out1, out3, out5, out7, out9, out10, out11, out12, out13, out14, out15
  Demultiplexer #(.enable("true"), .select(4)) demultiplexer_6 (
    .out4(demultiplexer_6_out4), .out6(demultiplexer_6_out6), .in(Start), .sel(Mode_FSM_1_mode), .en(1'b1));  // open: out0, out1, out2, out3, out5, out7, out8, out9, out10, out11, out12, out13, out14, out15
  xor xor_1 (xor_1_out, Stop_Alarm, Init_Impulse_1_reset);
  Clock Fifth_Sec_Clock (.out(Fifth_Sec_Clock_out));
  Mode_01_Time Mode_01_Time_1 (
    .Load(demultiplexer_5_out2), .Set_Next(demultiplexer_4_out2), .Set_UpDown(demultiplexer_2_out2),
    .Set_Count(demultiplexer_3_out2), .Reset_General(Reset), .Hour_10(Mode_01_Time_1_hour_10),
    .Hour_1(Mode_01_Time_1_hour_1), .Min_10(Mode_01_Time_1_min_10), .Min_1(Mode_01_Time_1_min_1),
    .Sec_10(Mode_01_Time_1_sec_10), .Sec_1(Mode_01_Time_1_sec_1), .Counting(Mode_01_Time_1_counting[0]),
    .Leds_Reset(Mode_01_Time_1_counting[1]), .Current_Hour(Mode_01_Time_1_current_hour),
    .Current_Minute(Mode_01_Time_1_current_minute), .Current_Second(Mode_01_Time_1_current_second));
  Mode_02_Chrono Mode_02_Chrono_1 (
    .Reset_Input(demultiplexer_5_out4), .Start_Pause(demultiplexer_6_out4),
    .Bascule_Reset(Init_Impulse_1_reset), .Reset_General(Reset), .Hour_10(Mode_02_Chrono_1_hour_10),
    .Hour_1(Mode_02_Chrono_1_hour_1), .Min_10(Mode_02_Chrono_1_min_10), .Min_1(Mode_02_Chrono_1_min_1),
    .Sec_10(Mode_02_Chrono_1_sec_10), .Sec_1(Mode_02_Chrono_1_sec_1),
    .Counting(Mode_02_Chrono_1_counting[0]), .Leds_Reset(Mode_02_Chrono_1_counting[1]));
  Mode_03_Timer Mode_03_Timer_1 (
    .StartsPause(demultiplexer_6_out6), .Load(demultiplexer_5_out6), .Set_Next(demultiplexer_4_out6),
    .Set_UpDown(demultiplexer_2_out6), .Set_Count(demultiplexer_3_out6),
    .Bascule_Reset(Init_Impulse_1_reset), .Stop_Alarm(xor_1_out), .Reset_General(Reset),
    .Hour_10(Mode_03_Timer_1_hour_10), .Hour_1(Mode_03_Timer_1_hour_1), .Min_10(Mode_03_Timer_1_min_10),
    .Min_1(Mode_03_Timer_1_min_1), .Sec_10(Mode_03_Timer_1_sec_10), .Sec_1(Mode_03_Timer_1_sec_1),
    .Counting(Mode_03_Timer_1_counting[0]), .Leds_Reset(Mode_03_Timer_1_counting[1]),
    .Buzzer_Output(Mode_03_Timer_1_buzzer_output));
  Mode_04_Alarm Mode_04_Alarm_1 (
    .Load(demultiplexer_5_out8), .Set_Next(demultiplexer_4_out8), .Set_UpDown(demultiplexer_2_out8),
    .Set_Count(demultiplexer_3_out8), .Hours(Mode_01_Time_1_current_hour),
    .Mins(Mode_01_Time_1_current_minute), .Secs(Mode_01_Time_1_current_second), .Stop_Alarm(xor_1_out),
    .Activate_Alarm(Actiavte_Alarm), .Bascule_Reset(Init_Impulse_1_reset), .Reset_General(Reset),
    .Hour_10(Mode_04_Alarm_1_hour_10), .Hour_1(Mode_04_Alarm_1_hour_1), .Min_10(Mode_04_Alarm_1_min_10),
    .Min_1(Mode_04_Alarm_1_min_1), .Sec_10(Mode_04_Alarm_1_sec_10), .Sec_1(Mode_04_Alarm_1_sec_1),
    .Buzzer(Mode_04_Alarm_1_buzzer));
  Message_HELLO Message_HELLO_1 (
    .Reset(demultiplexer_1_out0[1]), .Start(demultiplexer_1_out0[0]),
    .Output_To_Display(Message_HELLO_1_output_to_display), .Message_Done(Message_HELLO_1_message_done));
  D_Flip_Flop d_ff_1 (
    .D(Message_HELLO_1_message_done), .clk(Fifth_Sec_Clock_out), .Q(d_ff_5_q[4]), .preset(1'b0), .reset(1'b0));  // open: Qn
  Message_TIME Message_TIME_1 (
    .Reset(demultiplexer_1_out1[1]), .Start(demultiplexer_1_out1[0]),
    .Output_To_Display(Message_TIME_1_output_to_display), .Message_Done(Message_TIME_1_message_done));
  D_Flip_Flop d_ff_2 (
    .D(Message_TIME_1_message_done), .clk(Fifth_Sec_Clock_out), .Q(d_ff_5_q[3]), .preset(1'b0), .reset(1'b0));  // open: Qn
  Message_CHRONO Message_CHRONO_1 (
    .Reset(demultiplexer_1_out3[1]), .Start(demultiplexer_1_out3[0]),
    .Output_To_Display(Message_CHRONO_1_output_to_display), .Message_Done(Message_CHRONO_1_message_done));
  D_Flip_Flop d_ff_3 (
    .D(Message_CHRONO_1_message_done), .clk(Fifth_Sec_Clock_out), .Q(d_ff_5_q[2]), .preset(1'b0), .reset(1'b0));  // open: Qn
  Message_TIMER Message_TIMER_1 (
    .Reset(demultiplexer_1_out5[1]), .Start(demultiplexer_1_out5[0]),
    .Output_To_Display(Message_TIMER_1_output_to_display), .Message_Done(Message_TIMER_1_message_done));
  D_Flip_Flop d_ff_4 (
    .D(Message_TIMER_1_message_done), .clk(Fifth_Sec_Clock_out), .Q(d_ff_5_q[1]), .preset(1'b0), .reset(1'b0));  // open: Qn
  Message_ALARM Message_ALARM_1 (
    .Reset(demultiplexer_1_out7[1]), .Start(demultiplexer_1_out7[0]),
    .Output_To_Display(Message_ALARM_1_output_to_display), .Message_Done(Message_ALARM_1_message_done));
  D_Flip_Flop d_ff_5 (
    .D(Message_ALARM_1_message_done), .clk(Fifth_Sec_Clock_out), .Q(d_ff_5_q[0]), .preset(1'b0), .reset(1'b0));  // open: Qn
  Multiplexer #(.enable("true"), .select(4), .width(48)) multiplexer_1 (
    .in0(Message_HELLO_1_output_to_display), .in1(Message_TIME_1_output_to_display),
    .in2({Mode_01_Time_1_sec_1, Mode_01_Time_1_sec_10, Mode_01_Time_1_min_1, Mode_01_Time_1_min_10, Mode_01_Time_1_hour_1, Mode_01_Time_1_hour_10}),
    .in3(Message_CHRONO_1_output_to_display),
    .in4({Mode_02_Chrono_1_sec_1, Mode_02_Chrono_1_sec_10, Mode_02_Chrono_1_min_1, Mode_02_Chrono_1_min_10, Mode_02_Chrono_1_hour_1, Mode_02_Chrono_1_hour_10}),
    .in5(Message_TIMER_1_output_to_display),
    .in6({Mode_03_Timer_1_sec_1, Mode_03_Timer_1_sec_10, Mode_03_Timer_1_min_1, Mode_03_Timer_1_min_10, Mode_03_Timer_1_hour_1, Mode_03_Timer_1_hour_10}),
    .in7(Message_ALARM_1_output_to_display),
    .in8({Mode_04_Alarm_1_sec_1, Mode_04_Alarm_1_sec_10, Mode_04_Alarm_1_min_1, Mode_04_Alarm_1_min_10, Mode_04_Alarm_1_hour_1, Mode_04_Alarm_1_hour_10}),
    .in9({48{1'b0}}), .in10({48{1'b0}}), .in11({48{1'b0}}), .in12({48{1'b0}}), .in13({48{1'b0}}),
    .in14({48{1'b0}}), .in15({48{1'b0}}), .out(Display), .sel(Mode_FSM_1_mode), .en(1'b1));
  xor xor_2 (Buzzer_Output, Mode_03_Timer_1_buzzer_output, Mode_04_Alarm_1_buzzer);
  LtR_FSM LtR_FSM_1 (.Counting(Mode_01_Time_1_counting[0]), .Reset(Mode_01_Time_1_counting[1]), .LEDS(LtR_FSM_1_leds));
  LtR_FSM LtR_FSM_2 (
    .Counting(Mode_02_Chrono_1_counting[0]), .Reset(Mode_02_Chrono_1_counting[1]), .LEDS(LtR_FSM_2_leds));
  RtL_FSM RtL_FSM_1 (
    .Counting(Mode_03_Timer_1_counting[0]), .Reset(Mode_03_Timer_1_counting[1]), .LEDS(RtL_FSM_1_leds));
  Multiplexer #(.enable("true"), .select(4), .width(10)) multiplexer_2 (
    .in0({10{1'b0}}), .in1({10{1'b0}}), .in2(LtR_FSM_1_leds), .in3({10{1'b0}}), .in4(LtR_FSM_2_leds),
    .in5({10{1'b0}}), .in6(RtL_FSM_1_leds), .in7({10{1'b0}}), .in8({10{1'b0}}), .in9({10{1'b0}}),
    .in10({10{1'b0}}), .in11({10{1'b0}}), .in12({10{1'b0}}), .in13({10{1'b0}}), .in14({10{1'b0}}),
    .in15({10{1'b0}}), .out({LED_9, LED_8, LED_7, LED_6, LED_5, LED_4, LED_3, LED_2, LED_1, LED_0}),
    .sel(Mode_FSM_1_mode), .en(1'b1));
endmodule

module Mode_01_Time (
  input  Load,
  input  Set_Next,
  input  Set_UpDown,
  input  Set_Count,
  input  Reset_General,
  output [7:0] Hour_10,
  output [7:0] Hour_1,
  output [7:0] Min_10,
  output [7:0] Min_1,
  output [7:0] Sec_10,
  output [7:0] Sec_1,
  output Counting,
  output Leds_Reset,
  output [5:0] Current_Hour,
  output [5:0] Current_Minute,
  output [5:0] Current_Second
);

  wire and_1_out, and_2_out, blink_fsm_1_hour_source, blink_fsm_1_minute_source, blink_fsm_1_second_source,
       CentiSecondsClock_out, counter_4_carry, d_ff_1_q, d_ff_2_q, d_ff_3_q, demultiplexer_1_out0,
       demultiplexer_1_out1, demultiplexer_1_out2, KHzClock_out, MinuteCounter_carry, SecondsCounter_carry;
  wire [1:0] III_Cycler_FSM_1_mode;
  wire [5:0] counter_1_q, counter_2_q, counter_3_q, multiplexer_1_out, multiplexer_2_out, multiplexer_3_out;
  wire [6:0] bcd_to_7_segment_decoder_1_p3, bcd_to_7_segment_decoder_2_p3, bcd_to_7_segment_decoder_3_p3,
       bcd_to_7_segment_decoder_4_p5, bcd_to_7_segment_decoder_5_p5, bcd_to_7_segment_decoder_6_p5;

  Clock KHzClock (.out(KHzClock_out));
  Clock #(.highDuration(5), .lowDuration(5)) CentiSecondsClock (.out(CentiSecondsClock_out));
  III_Cycler_FSM III_Cycler_FSM_1 (.Switch(Set_Next), .Mode(III_Cycler_FSM_1_mode));
  Demultiplexer #(.enable("true"), .select(2)) demultiplexer_1 (
    .out0(demultiplexer_1_out0), .out1(demultiplexer_1_out1), .out2(demultiplexer_1_out2), .in(Set_Count),
    .sel(III_Cycler_FSM_1_mode), .en(1'b1));  // open: out3
  D_Flip_Flop d_ff_1 (
    .D(demultiplexer_1_out2), .clk(KHzClock_out), .Q(d_ff_1_q), .preset(1'b0), .reset(1'b0));  // open: Qn
  D_Flip_Flop d_ff_2 (
    .D(demultiplexer_1_out1), .clk(KHzClock_out), .Q(d_ff_2_q), .preset(1'b0), .reset(1'b0));  // open: Qn
  D_Flip_Flop d_ff_3 (
    .D(demultiplexer_1_out0), .clk(KHzClock_out), .Q(d_ff_3_q), .preset(1'b0), .reset(1'b0));  // open: Qn
  Counter #(.max('h17), .trigger("falling"), .width(6)) counter_1 (
    .clr(Reset_General), .load(1'b0), .up(Set_UpDown), .count(d_ff_1_q), .clk(KHzClock_out), .D({6{1'b0}}),
    .Q(counter_1_q));  // open: carry
  Counter #(.max('h3b), .trigger("falling"), .width(6)) counter_2 (
    .clr(Reset_General), .load(1'b0), .up(Set_UpDown), .count(d_ff_2_q), .clk(KHzClock_out), .D({6{1'b0}}),
    .Q(counter_2_q));  // open: carry
  Counter #(.max('h3b), .trigger("falling"), .width(6)) counter_3 (
    .clr(Reset_General), .load(1'b0), .up(Set_UpDown), .count(d_ff_3_q), .clk(KHzClock_out), .D({6{1'b0}}),
    .Q(counter_3_q));  // open: carry
  and and_1 (and_1_out, and_2_out, MinuteCounter_carry);
  and and_2 (and_2_out, counter_4_carry, SecondsCounter_carry);
  Counter #(.max('h17), .trigger("falling"), .width(6)) HourCounter (
    .clr(Reset_General), .load(Load), .up(1'b1), .count(and_1_out), .clk(CentiSecondsClock_out),
    .D(counter_1_q), .Q(Current_Hour));  // open: carry
  Counter #(.max('h3b), .trigger("falling"), .width(6)) MinuteCounter (
    .clr(Reset_General), .load(Load), .up(1'b1), .count(and_2_out), .clk(CentiSecondsClock_out),
    .D(counter_2_q), .carry(MinuteCounter_carry), .Q(Current_Minute));
  Counter #(.max('h3b), .trigger("falling"), .width(6)) SecondsCounter (
    .clr(Reset_General), .load(Load), .up(1'b1), .count(counter_4_carry), .clk(CentiSecondsClock_out),
    .D(counter_3_q), .carry(SecondsCounter_carry), .Q(Current_Second));
  Counter #(.max('h63), .trigger("falling")) counter_4 (
    .clr(Reset_General), .load(1'b0), .up(1'b1), .count(1'b1), .clk(CentiSecondsClock_out), .D({8{1'b0}}),
    .carry(counter_4_carry));  // open: Q
  // BCD_to_7_Segment_decoder bcd_to_7_segment_decoder_1: pin names not known; wires that end beside it: bcd_to_7_segment_decoder_1_p3[6], bcd_to_7_segment_decoder_1_p3[5], bcd_to_7_segment_decoder_1_p3[0], bcd_to_7_segment_decoder_1_p3[1]
  Multiplexer #(.enable("true"), .width(6)) multiplexer_1 (
    .in0(Current_Hour), .in1(counter_1_q), .out(multiplexer_1_out), .sel(Load), .en(1'b1));
  // Binary_to_BCD_converter #(.binvalue(6)) binary_to_bcd_converter_1: pin names not known; wires that end beside it: multiplexer_1_out, bcd_to_7_segment_decoder_1_p3[4], bcd_to_7_segment_decoder_1_p3[3], bcd_to_7_segment_decoder_1_p3[2]
  // BCD_to_7_Segment_decoder bcd_to_7_segment_decoder_2: pin names not known; wires that end beside it: bcd_to_7_segment_decoder_2_p3[6], bcd_to_7_segment_decoder_2_p3[5], bcd_to_7_segment_decoder_2_p3[0], bcd_to_7_segment_decoder_2_p3[1]
  Multiplexer #(.enable("true"), .width(6)) multiplexer_2 (
    .in0(Current_Minute), .in1(counter_2_q), .out(multiplexer_2_out), .sel(Load), .en(1'b1));
  // Binary_to_BCD_converter #(.binvalue(6)) binary_to_bcd_converter_2: pin names not known; wires that end beside it: multiplexer_2_out, bcd_to_7_segment_decoder_2_p3[4], bcd_to_7_segment_decoder_2_p3[3], bcd_to_7_segment_decoder_2_p3[2]
  // BCD_to_7_Segment_decoder bcd_to_7_segment_decoder_3: pin names not known; wires that end beside it: bcd_to_7_segment_decoder_3_p3[6], bcd_to_7_segment_decoder_3_p3[5], bcd_to_7_segment_decoder_3_p3[0], bcd_to_7_segment_decoder_3_p3[1]
  Multiplexer #(.enable("true"), .width(6)) multiplexer_3 (
    .in0(Current_Second), .in1(counter_3_q), .out(multiplexer_3_out), .sel(Load), .en(1'b1));
  // Binary_to_BCD_converter #(.binvalue(6)) binary_to_bcd_converter_3: pin names not known; wires that end beside it: multiplexer_3_out, bcd_to_7_segment_decoder_3_p3[4], bcd_to_7_segment_decoder_3_p3[3], bcd_to_7_segment_decoder_3_p3[2]
  // BCD_to_7_Segment_decoder bcd_to_7_segment_decoder_4: pin names not known; wires that end beside it: bcd_to_7_segment_decoder_4_p5[6], bcd_to_7_segment_decoder_4_p5[4], bcd_to_7_segment_decoder_4_p5[5], bcd_to_7_segment_decoder_4_p5[3], bcd_to_7_segment_decoder_4_p5[0], bcd_to_7_segment_decoder_4_p5[2], bcd_to_7_segment_decoder_4_p5[1]
  // BCD_to_7_Segment_decoder bcd_to_7_segment_decoder_5: pin names not known; wires that end beside it: bcd_to_7_segment_decoder_5_p5[6], bcd_to_7_segment_decoder_5_p5[4], bcd_to_7_segment_decoder_5_p5[5], bcd_to_7_segment_decoder_5_p5[3], bcd_to_7_segment_decoder_5_p5[0], bcd_to_7_segment_decoder_5_p5[2], bcd_to_7_segment_decoder_5_p5[1]
  // BCD_to_7_Segment_decoder bcd_to_7_segment_decoder_6: pin names not known; wires that end beside it: bcd_to_7_segment_decoder_6_p5[6], bcd_to_7_segment_decoder_6_p5[4], bcd_to_7_segment_decoder_6_p5[5], bcd_to_7_segment_decoder_6_p5[3], bcd_to_7_segment_decoder_6_p5[0], bcd_to_7_segment_decoder_6_p5[2], bcd_to_7_segment_decoder_6_p5[1]
  Blink_FSM blink_fsm_1 (
    .Reset(Set_Count), .Load(Load), .Mode(III_Cycler_FSM_1_mode), .Second_Source(blink_fsm_1_second_source),
    .Minute_Source(blink_fsm_1_minute_source), .Hour_Source(blink_fsm_1_hour_source));
  not not_1 (Counting, Load);
  or or_1 (Leds_Reset, Load, counter_4_carry, Reset_General);
  Multiplexer #(.width(8)) multiplexer_4 (
    .in0({8{1'b0}}), .in1({1'b0, bcd_to_7_segment_decoder_1_p3}), .out(Hour_10), .sel(blink_fsm_1_hour_source));
  Multiplexer #(.width(8)) multiplexer_5 (
    .in0({8{1'b0}}), .in1({1'b1, bcd_to_7_segment_decoder_4_p5}), .out(Hour_1), .sel(blink_fsm_1_hour_source));
  Multiplexer #(.width(8)) multiplexer_6 (
    .in0({8{1'b0}}), .in1({1'b0, bcd_to_7_segment_decoder_2_p3}), .out(Min_10),
    .sel(blink_fsm_1_minute_source));
  Multiplexer #(.width(8)) multiplexer_7 (
    .in0({8{1'b0}}), .in1({1'b1, bcd_to_7_segment_decoder_5_p5}), .out(Min_1), .sel(blink_fsm_1_minute_source));
  Multiplexer #(.width(8)) multiplexer_8 (
    .in0({8{1'b0}}), .in1({1'b0, bcd_to_7_segment_decoder_3_p3}), .out(Sec_10),
    .sel(blink_fsm_1_second_source));
  Multiplexer #(.width(8)) multiplexer_9 (
    .in0({8{1'b0}}), .in1({1'b0, bcd_to_7_segment_decoder_6_p5}), .out(Sec_1), .sel(blink_fsm_1_second_source));
endmodule

module Mode_02_Chrono (
  input  Reset_Input,
  input  Start_Pause,
  input  Bascule_Reset,
  input  Reset_General,
  output [7:0] Hour_10,
  output [7:0] Hour_1,
  output [7:0] Min_10,
  output [7:0] Min_1,
  output [7:0] Sec_10,
  output [7:0] Sec_1,
  output Counting,
  output Leds_Reset
);

  wire and_1_out, and_2_out, and_3_out, clock_1_out, counter_2_carry, counter_3_carry, not_1_out, or_1_out,
       or_2_out;
  wire [5:0] counter_2_q;
  wire [6:0] counter_1_q, counter_3_q;

  Clock #(.highDuration(5), .lowDuration(5)) clock_1 (.out(clock_1_out));
  or or_1 (or_1_out, Bascule_Reset, Reset_General);
  Bascule_FSM Bascule_FSM_1 (.Bascule_Output(Counting), .Reset(or_1_out), .Switch(Start_Pause));
  and and_1 (and_1_out, Reset_Input, not_1_out);
  not not_1 (not_1_out, Counting);
  and and_2 (and_2_out, and_3_out, counter_2_carry);
  and and_3 (and_3_out, Counting, counter_3_carry);
  or or_2 (or_2_out, Reset_General, and_1_out);
  Counter #(.max('h63), .width(7)) counter_1 (
    .clr(or_2_out), .load(1'b0), .up(1'b1), .count(and_2_out), .clk(clock_1_out), .D({7{1'b0}}),
    .Q(counter_1_q));  // open: carry
  Counter #(.max('h3b), .width(6)) counter_2 (
    .clr(or_2_out), .load(1'b0), .up(1'b1), .count(and_3_out), .clk(clock_1_out), .D({6{1'b0}}),
    .carry(counter_2_carry), .Q(counter_2_q));
  Counter #(.max('h63), .width(7)) counter_3 (
    .clr(or_2_out), .load(1'b0), .up(1'b1), .count(Counting), .clk(clock_1_out), .D({7{1'b0}}),
    .carry(counter_3_carry), .Q(counter_3_q));
  // Binary_to_BCD_converter #(.binvalue(7)) binary_to_bcd_converter_1: pin names not known; wires that end beside it: counter_1_q
  // Binary_to_BCD_converter #(.binvalue(7)) binary_to_bcd_converter_2: pin names not known; wires that end beside it: counter_3_q
  // BCD_to_7_Segment_decoder bcd_to_7_segment_decoder_1: pin names not known; wires that end beside it: Hour_10[6], Hour_10[4], Hour_10[5], Hour_10[3], Hour_10[0], Hour_10[2], Hour_10[1]
  // BCD_to_7_Segment_decoder bcd_to_7_segment_decoder_2: pin names not known; wires that end beside it: Min_10[6], Min_10[5], Min_10[0], Min_10[1]
  // Binary_to_BCD_converter #(.binvalue(6)) binary_to_bcd_converter_3: pin names not known; wires that end beside it: counter_2_q, Min_10[4], Min_10[3], Min_10[2]
  // BCD_to_7_Segment_decoder bcd_to_7_segment_decoder_3: pin names not known; wires that end beside it: Sec_10[6], Sec_10[4], Sec_10[5], Sec_10[3], Sec_10[0], Sec_10[2], Sec_10[1]
  // BCD_to_7_Segment_decoder bcd_to_7_segment_decoder_4: pin names not known; wires that end beside it: Hour_1[6], Hour_1[4], Hour_1[5], Hour_1[3], Hour_1[0], Hour_1[2], Hour_1[1]
  // BCD_to_7_Segment_decoder bcd_to_7_segment_decoder_5: pin names not known; wires that end beside it: Min_1[6], Min_1[4], Min_1[5], Min_1[3], Min_1[0], Min_1[2], Min_1[1]
  // BCD_to_7_Segment_decoder bcd_to_7_segment_decoder_6: pin names not known; wires that end beside it: Sec_1[6], Sec_1[4], Sec_1[5], Sec_1[3], Sec_1[0], Sec_1[2], Sec_1[1]
  or or_3 (Leds_Reset, counter_3_carry, or_2_out);

  assign Hour_1[7] = 1'b1;
  assign Hour_10[7] = 1'b0;
  assign Min_1[7] = 1'b1;
  assign Min_10[7] = 1'b0;
  assign Sec_1[7] = 1'b0;
  assign Sec_10[7] = 1'b0;
endmodule

module Mode_03_Timer (
  input  StartsPause,
  input  Load,
  input  Set_Next,
  input  Set_UpDown,
  input  Set_Count,
  input  Bascule_Reset,
  input  Stop_Alarm,
  input  Reset_General,
  output [7:0] Hour_10,
  output [7:0] Hour_1,
  output [7:0] Min_10,
  output [7:0] Min_1,
  output [7:0] Sec_10,
  output [7:0] Sec_1,
  output Counting,
  output Leds_Reset,
  output Buzzer_Output
);

  wire and_1_out, and_2_out, and_3_out, and_4_out, and_5_out, and_6_out, and_7_out, and_8_out,
       Bascule_FSM_1_bascule_output, blink_fsm_1_hour_source, blink_fsm_1_minute_source,
       blink_fsm_1_second_source, clock_1_out, counter_5_carry, counter_6_carry, counter_7_carry, d_ff_1_q,
       d_ff_3_q, d_ff_4_q, d_ff_5_q, demultiplexer_1_out0, demultiplexer_1_out1, demultiplexer_1_out2,
       Impulse_1_impulse_response, KHz_Clock_out, Mili_Seconds_Clock_out, Mode_03_TimerInput_FSM_1_g5,
       Mode_03_TimerInput_FSM_1_m1, multiplexer_4_out, multiplexer_11_out, not_1_out, not_2_out, not_3_out,
       not_4_out, not_5_out, not_6_out, not_7_out, not_8_out, not_9_out, not_10_out, not_11_out, not_12_out,
       not_13_out, not_14_out, not_15_out, not_16_out, not_17_out, not_18_out, not_19_out, not_20_out,
       or_1_out, Sequence_Hz_out, Sound_Hz_out, Time_Bascule_FSM_buzzer;
  wire [1:0] III_Cycler_FSM_1_mode;
  wire [5:0] counter_2_q, counter_3_q, counter_5_q, counter_6_q, multiplexer_2_out, multiplexer_3_out;
  wire [6:0] bcd_to_7_segment_decoder_1_p3, bcd_to_7_segment_decoder_2_p3, bcd_to_7_segment_decoder_3_p5,
       bcd_to_7_segment_decoder_4_p5, bcd_to_7_segment_decoder_5_p5, bcd_to_7_segment_decoder_6_p5,
       counter_1_q, counter_4_q, multiplexer_1_out;

  Impulse Impulse_1 (.Impulse_Response(Impulse_1_impulse_response), .Activation(and_5_out));
  or or_1 (or_1_out, Impulse_1_impulse_response, StartsPause);
  Bascule_FSM Bascule_FSM_1 (.Bascule_Output(Bascule_FSM_1_bascule_output), .Reset(Bascule_Reset), .Switch(or_1_out));
  III_Cycler_FSM III_Cycler_FSM_1 (.Switch(Set_Next), .Mode(III_Cycler_FSM_1_mode));
  Mode_03_TimerInput_FSM Mode_03_TimerInput_FSM_1 (
    .Done(and_5_out), .StartPause(Bascule_FSM_1_bascule_output), .Load(Load), .CurrentStart(Counting),
    .CurrentLoad(d_ff_1_q), .M1(Mode_03_TimerInput_FSM_1_m1), .G5(Mode_03_TimerInput_FSM_1_g5));
  Demultiplexer #(.enable("true"), .select(2)) demultiplexer_1 (
    .out0(demultiplexer_1_out0), .out1(demultiplexer_1_out1), .out2(demultiplexer_1_out2), .in(Set_Count),
    .sel(III_Cycler_FSM_1_mode), .en(1'b1));  // open: out3
  Clock KHz_Clock (.out(KHz_Clock_out));
  D_Flip_Flop d_ff_1 (
    .D(Mode_03_TimerInput_FSM_1_m1), .clk(KHz_Clock_out), .Q(d_ff_1_q), .preset(1'b0), .reset(1'b0));  // open: Qn
  D_Flip_Flop d_ff_2 (
    .D(Mode_03_TimerInput_FSM_1_g5), .clk(KHz_Clock_out), .Q(Counting), .preset(1'b0), .reset(1'b0));  // open: Qn
  D_Flip_Flop d_ff_3 (
    .D(demultiplexer_1_out2), .clk(KHz_Clock_out), .Q(d_ff_3_q), .preset(1'b0), .reset(1'b0));  // open: Qn
  D_Flip_Flop d_ff_4 (
    .D(demultiplexer_1_out1), .clk(KHz_Clock_out), .Q(d_ff_4_q), .preset(1'b0), .reset(1'b0));  // open: Qn
  D_Flip_Flop d_ff_5 (
    .D(demultiplexer_1_out0), .clk(KHz_Clock_out), .Q(d_ff_5_q), .preset(1'b0), .reset(1'b0));  // open: Qn
  Counter #(.max('h63), .trigger("falling"), .width(7)) counter_1 (
    .clr(Reset_General), .load(1'b0), .up(Set_UpDown), .count(d_ff_3_q), .clk(KHz_Clock_out), .D({7{1'b0}}),
    .Q(counter_1_q));  // open: carry
  Counter #(.max('h3b), .trigger("falling"), .width(6)) counter_2 (
    .clr(Reset_General), .load(1'b0), .up(Set_UpDown), .count(d_ff_4_q), .clk(KHz_Clock_out), .D({6{1'b0}}),
    .Q(counter_2_q));  // open: carry
  Counter #(.max('h3b), .trigger("falling"), .width(6)) counter_3 (
    .clr(Reset_General), .load(1'b0), .up(Set_UpDown), .count(d_ff_5_q), .clk(KHz_Clock_out), .D({6{1'b0}}),
    .Q(counter_3_q));  // open: carry
  Clock #(.highDuration(5), .lowDuration(5), .phaseOffset(5)) Mili_Seconds_Clock (.out(Mili_Seconds_Clock_out));
  and and_1 (and_1_out, and_2_out, counter_5_carry);
  and and_2 (and_2_out, and_3_out, counter_6_carry);
  and and_3 (and_3_out, and_4_out, counter_7_carry);
  and and_4 (and_4_out, Counting, not_1_out);
  not not_1 (not_1_out, and_5_out);
  Counter #(.max('h63), .ongoal("stay"), .width(7)) counter_4 (
    .clr(Reset_General), .load(d_ff_1_q), .up(1'b0), .count(and_1_out), .clk(Mili_Seconds_Clock_out),
    .D(counter_1_q), .Q(counter_4_q));  // open: carry
  Counter #(.max('h3b), .width(6)) counter_5 (
    .clr(Reset_General), .load(d_ff_1_q), .up(1'b0), .count(and_2_out), .clk(Mili_Seconds_Clock_out),
    .D(counter_2_q), .carry(counter_5_carry), .Q(counter_5_q));
  Counter #(.max('h3b), .width(6)) counter_6 (
    .clr(Reset_General), .load(d_ff_1_q), .up(1'b0), .count(and_3_out), .clk(Mili_Seconds_Clock_out),
    .D(counter_3_q), .carry(counter_6_carry), .Q(counter_6_q));
  Counter #(.max('h63), .width(7)) counter_7 (
    .clr(Reset_General), .load(d_ff_1_q), .up(1'b1), .count(and_4_out), .clk(Mili_Seconds_Clock_out),
    .D({7{1'b0}}), .carry(counter_7_carry));  // open: Q
  and and_5 (and_5_out, and_6_out, and_7_out, and_8_out);
  and and_6 (and_6_out, not_2_out, not_3_out, not_4_out, not_5_out, not_6_out, not_7_out, not_8_out);
  and and_7 (and_7_out, not_9_out, not_10_out, not_11_out, not_12_out, not_13_out, not_14_out);
  and and_8 (and_8_out, not_15_out, not_16_out, not_17_out, not_18_out, not_19_out, not_20_out);
  not not_2 (not_2_out, counter_4_q[0]);
  not not_3 (not_3_out, counter_4_q[1]);
  not not_4 (not_4_out, counter_4_q[2]);
  not not_5 (not_5_out, counter_4_q[3]);
  not not_6 (not_6_out, counter_4_q[4]);
  not not_7 (not_7_out, counter_4_q[5]);
  not not_8 (not_8_out, counter_4_q[6]);
  not not_9 (not_9_out, counter_5_q[0]);
  not not_10 (not_10_out, counter_5_q[1]);
  not not_11 (not_11_out, counter_5_q[2]);
  not not_12 (not_12_out, counter_5_q[3]);
  not not_13 (not_13_out, counter_5_q[4]);
  not not_14 (not_14_out, counter_5_q[5]);
  not not_15 (not_15_out, counter_6_q[0]);
  not not_16 (not_16_out, counter_6_q[1]);
  not not_17 (not_17_out, counter_6_q[2]);
  not not_18 (not_18_out, counter_6_q[3]);
  not not_19 (not_19_out, counter_6_q[4]);
  not not_20 (not_20_out, counter_6_q[5]);
  Multiplexer #(.enable("true"), .width(7)) multiplexer_1 (
    .in0(counter_4_q), .in1(counter_1_q), .out(multiplexer_1_out), .sel(d_ff_1_q), .en(1'b1));
  Multiplexer #(.enable("true"), .width(6)) multiplexer_2 (
    .in0(counter_5_q), .in1(counter_2_q), .out(multiplexer_2_out), .sel(d_ff_1_q), .en(1'b1));
  Multiplexer #(.enable("true"), .width(6)) multiplexer_3 (
    .in0(counter_6_q), .in1(counter_3_q), .out(multiplexer_3_out), .sel(d_ff_1_q), .en(1'b1));
  // Binary_to_BCD_converter #(.binvalue(7)) binary_to_bcd_converter_1: pin names not known; wires that end beside it: multiplexer_1_out
  // BCD_to_7_Segment_decoder bcd_to_7_segment_decoder_1: pin names not known; wires that end beside it: bcd_to_7_segment_decoder_1_p3[6], bcd_to_7_segment_decoder_1_p3[5], bcd_to_7_segment_decoder_1_p3[0], bcd_to_7_segment_decoder_1_p3[1]
  // Binary_to_BCD_converter #(.binvalue(6)) binary_to_bcd_converter_2: pin names not known; wires that end beside it: multiplexer_2_out, bcd_to_7_segment_decoder_1_p3[4], bcd_to_7_segment_decoder_1_p3[3], bcd_to_7_segment_decoder_1_p3[2]
  // BCD_to_7_Segment_decoder bcd_to_7_segment_decoder_2: pin names not known; wires that end beside it: bcd_to_7_segment_decoder_2_p3[6], bcd_to_7_segment_decoder_2_p3[5], bcd_to_7_segment_decoder_2_p3[0], bcd_to_7_segment_decoder_2_p3[1]
  // Binary_to_BCD_converter #(.binvalue(6)) binary_to_bcd_converter_3: pin names not known; wires that end beside it: multiplexer_3_out, bcd_to_7_segment_decoder_2_p3[4], bcd_to_7_segment_decoder_2_p3[3], bcd_to_7_segment_decoder_2_p3[2]
  // BCD_to_7_Segment_decoder bcd_to_7_segment_decoder_3: pin names not known; wires that end beside it: bcd_to_7_segment_decoder_3_p5[6], bcd_to_7_segment_decoder_3_p5[4], bcd_to_7_segment_decoder_3_p5[5], bcd_to_7_segment_decoder_3_p5[3], bcd_to_7_segment_decoder_3_p5[0], bcd_to_7_segment_decoder_3_p5[2], bcd_to_7_segment_decoder_3_p5[1]
  // BCD_to_7_Segment_decoder bcd_to_7_segment_decoder_4: pin names not known; wires that end beside it: bcd_to_7_segment_decoder_4_p5[6], bcd_to_7_segment_decoder_4_p5[4], bcd_to_7_segment_decoder_4_p5[5], bcd_to_7_segment_decoder_4_p5[3], bcd_to_7_segment_decoder_4_p5[0], bcd_to_7_segment_decoder_4_p5[2], bcd_to_7_segment_decoder_4_p5[1]
  // BCD_to_7_Segment_decoder bcd_to_7_segment_decoder_5: pin names not known; wires that end beside it: bcd_to_7_segment_decoder_5_p5[6], bcd_to_7_segment_decoder_5_p5[4], bcd_to_7_segment_decoder_5_p5[5], bcd_to_7_segment_decoder_5_p5[3], bcd_to_7_segment_decoder_5_p5[0], bcd_to_7_segment_decoder_5_p5[2], bcd_to_7_segment_decoder_5_p5[1]
  or or_2 (Leds_Reset, d_ff_1_q, and_2_out, Reset_General);
  // BCD_to_7_Segment_decoder bcd_to_7_segment_decoder_6: pin names not known; wires that end beside it: bcd_to_7_segment_decoder_6_p5[6], bcd_to_7_segment_decoder_6_p5[4], bcd_to_7_segment_decoder_6_p5[5], bcd_to_7_segment_decoder_6_p5[3], bcd_to_7_segment_decoder_6_p5[0], bcd_to_7_segment_decoder_6_p5[2], bcd_to_7_segment_decoder_6_p5[1]
  Clock #(.highDuration(62), .lowDuration(63)) Sequence_Hz (.out(Sequence_Hz_out));
  Clock Sound_Hz (.out(Sound_Hz_out));
  Blink_FSM blink_fsm_1 (
    .Reset(Set_Count), .Load(d_ff_1_q), .Mode(III_Cycler_FSM_1_mode),
    .Second_Source(blink_fsm_1_second_source), .Minute_Source(blink_fsm_1_minute_source),
    .Hour_Source(blink_fsm_1_hour_source));
  Timer_Buzzer_FSM Time_Bascule_FSM (
    .Stop(Stop_Alarm), .Is_Time(and_5_out), .Start(StartsPause), .Reset_General(Reset_General),
    .Buzzer(Time_Bascule_FSM_buzzer));
  Clock #(.highDuration(500), .lowDuration(500)) clock_1 (.out(clock_1_out));
  Multiplexer multiplexer_4 (.in0(1'b0), .in1(Sound_Hz_out), .out(multiplexer_4_out), .sel(Sequence_Hz_out));
  Multiplexer #(.width(8)) multiplexer_5 (
    .in0({8{1'b0}}), .in1({1'b0, bcd_to_7_segment_decoder_3_p5}), .out(Hour_10), .sel(blink_fsm_1_hour_source));
  Multiplexer #(.width(8)) multiplexer_6 (
    .in0({8{1'b0}}), .in1({1'b1, bcd_to_7_segment_decoder_6_p5}), .out(Hour_1), .sel(blink_fsm_1_hour_source));
  Multiplexer #(.width(8)) multiplexer_7 (
    .in0({8{1'b0}}), .in1({1'b0, bcd_to_7_segment_decoder_1_p3}), .out(Min_10),
    .sel(blink_fsm_1_minute_source));
  Multiplexer #(.width(8)) multiplexer_8 (
    .in0({8{1'b0}}), .in1({1'b1, bcd_to_7_segment_decoder_4_p5}), .out(Min_1), .sel(blink_fsm_1_minute_source));
  Multiplexer #(.width(8)) multiplexer_9 (
    .in0({8{1'b0}}), .in1({1'b0, bcd_to_7_segment_decoder_2_p3}), .out(Sec_10),
    .sel(blink_fsm_1_second_source));
  Multiplexer #(.width(8)) multiplexer_10 (
    .in0({8{1'b0}}), .in1({1'b0, bcd_to_7_segment_decoder_5_p5}), .out(Sec_1), .sel(blink_fsm_1_second_source));
  Multiplexer multiplexer_11 (.in0(1'b0), .in1(multiplexer_4_out), .out(multiplexer_11_out), .sel(clock_1_out));
  and and_9 (Buzzer_Output, Time_Bascule_FSM_buzzer, multiplexer_11_out);
endmodule

module Mode_04_Alarm (
  input  Load,
  input  Set_Next,
  input  Set_UpDown,
  input  Set_Count,
  input  [5:0] Hours,
  input  [5:0] Mins,
  input  [5:0] Secs,
  input  Stop_Alarm,
  input  Activate_Alarm,
  input  Bascule_Reset,
  input  Reset_General,
  output [7:0] Hour_10,
  output [7:0] Hour_1,
  output [7:0] Min_10,
  output [7:0] Min_1,
  output [7:0] Sec_10,
  output [7:0] Sec_1,
  output Buzzer
);

  wire and_1_out, Bascule_Alarm_FSM_1_buzzer_active, blink_fsm_1_hour_source, blink_fsm_1_minute_source,
       blink_fsm_1_second_source, clock_1_out, comparator_1_eq, comparator_2_eq, comparator_3_eq, d_ff_1_q,
       d_ff_2_q, d_ff_3_q, demultiplexer_1_out0, demultiplexer_1_out1, demultiplexer_1_out2, not_1_out,
       or_1_out;
  wire [1:0] III_Cycler_FSM_1_mode;
  wire [5:0] counter_1_q, counter_2_q, counter_3_q, multiplexer_1_out, multiplexer_2_out, multiplexer_3_out;
  wire [6:0] bcd_to_7_segment_decoder_1_p3, bcd_to_7_segment_decoder_2_p5, bcd_to_7_segment_decoder_3_p3,
       bcd_to_7_segment_decoder_4_p5, bcd_to_7_segment_decoder_5_p3, bcd_to_7_segment_decoder_6_p5;

  III_Cycler_FSM III_Cycler_FSM_1 (.Switch(Set_Next), .Mode(III_Cycler_FSM_1_mode));
  Demultiplexer #(.enable("true"), .select(2)) demultiplexer_1 (
    .out0(demultiplexer_1_out0), .out1(demultiplexer_1_out1), .out2(demultiplexer_1_out2), .in(Set_Count),
    .sel(III_Cycler_FSM_1_mode), .en(1'b1));  // open: out3
  Clock clock_1 (.out(clock_1_out));
  D_Flip_Flop d_ff_1 (
    .D(demultiplexer_1_out2), .clk(clock_1_out), .Q(d_ff_1_q), .preset(1'b0), .reset(1'b0));  // open: Qn
  D_Flip_Flop d_ff_2 (
    .D(demultiplexer_1_out1), .clk(clock_1_out), .Q(d_ff_2_q), .preset(1'b0), .reset(1'b0));  // open: Qn
  D_Flip_Flop d_ff_3 (
    .D(demultiplexer_1_out0), .clk(clock_1_out), .Q(d_ff_3_q), .preset(1'b0), .reset(1'b0));  // open: Qn
  Counter #(.max('h17), .trigger("falling"), .width(6)) counter_1 (
    .clr(Reset_General), .load(1'b0), .up(Set_UpDown), .count(d_ff_1_q), .clk(clock_1_out), .D(6'b001100),
    .Q(counter_1_q));  // open: carry
  Counter #(.max('h3b), .trigger("falling"), .width(6)) counter_2 (
    .clr(Reset_General), .load(1'b0), .up(Set_UpDown), .count(d_ff_2_q), .clk(clock_1_out), .D({6{1'b0}}),
    .Q(counter_2_q));  // open: carry
  Counter #(.max('h3b), .trigger("falling"), .width(6)) counter_3 (
    .clr(Reset_General), .load(1'b0), .up(Set_UpDown), .count(d_ff_3_q), .clk(clock_1_out), .D({6{1'b0}}),
    .Q(counter_3_q));  // open: carry
  not not_1 (not_1_out, Load);
  Multiplexer #(.enable("true"), .width(6)) multiplexer_1 (
    .in0(counter_1_q), .in1(Hours), .out(multiplexer_1_out), .sel(not_1_out), .en(1'b1));
  Multiplexer #(.enable("true"), .width(6)) multiplexer_2 (
    .in0(counter_2_q), .in1(Mins), .out(multiplexer_2_out), .sel(not_1_out), .en(1'b1));
  Multiplexer #(.enable("true"), .width(6)) multiplexer_3 (
    .in0(counter_3_q), .in1(Secs), .out(multiplexer_3_out), .sel(not_1_out), .en(1'b1));
  // BCD_to_7_Segment_decoder bcd_to_7_segment_decoder_1: pin names not known; wires that end beside it: bcd_to_7_segment_decoder_1_p3[6], bcd_to_7_segment_decoder_1_p3[5], bcd_to_7_segment_decoder_1_p3[0], bcd_to_7_segment_decoder_1_p3[1]
  // BCD_to_7_Segment_decoder bcd_to_7_segment_decoder_2: pin names not known; wires that end beside it: bcd_to_7_segment_decoder_2_p5[6], bcd_to_7_segment_decoder_2_p5[4], bcd_to_7_segment_decoder_2_p5[5], bcd_to_7_segment_decoder_2_p5[3], bcd_to_7_segment_decoder_2_p5[0], bcd_to_7_segment_decoder_2_p5[2], bcd_to_7_segment_decoder_2_p5[1]
  // Binary_to_BCD_converter #(.binvalue(6)) binary_to_bcd_converter_1: pin names not known; wires that end beside it: multiplexer_1_out, bcd_to_7_segment_decoder_1_p3[4], bcd_to_7_segment_decoder_1_p3[3], bcd_to_7_segment_decoder_1_p3[2]
  // BCD_to_7_Segment_decoder bcd_to_7_segment_decoder_3: pin names not known; wires that end beside it: bcd_to_7_segment_decoder_3_p3[6], bcd_to_7_segment_decoder_3_p3[5], bcd_to_7_segment_decoder_3_p3[0], bcd_to_7_segment_decoder_3_p3[1]
  // BCD_to_7_Segment_decoder bcd_to_7_segment_decoder_4: pin names not known; wires that end beside it: bcd_to_7_segment_decoder_4_p5[6], bcd_to_7_segment_decoder_4_p5[4], bcd_to_7_segment_decoder_4_p5[5], bcd_to_7_segment_decoder_4_p5[3], bcd_to_7_segment_decoder_4_p5[0], bcd_to_7_segment_decoder_4_p5[2], bcd_to_7_segment_decoder_4_p5[1]
  // Binary_to_BCD_converter #(.binvalue(6)) binary_to_bcd_converter_2: pin names not known; wires that end beside it: multiplexer_2_out, bcd_to_7_segment_decoder_3_p3[4], bcd_to_7_segment_decoder_3_p3[3], bcd_to_7_segment_decoder_3_p3[2]
  // BCD_to_7_Segment_decoder bcd_to_7_segment_decoder_5: pin names not known; wires that end beside it: bcd_to_7_segment_decoder_5_p3[6], bcd_to_7_segment_decoder_5_p3[5], bcd_to_7_segment_decoder_5_p3[0], bcd_to_7_segment_decoder_5_p3[1]
  // BCD_to_7_Segment_decoder bcd_to_7_segment_decoder_6: pin names not known; wires that end beside it: bcd_to_7_segment_decoder_6_p5[6], bcd_to_7_segment_decoder_6_p5[4], bcd_to_7_segment_decoder_6_p5[5], bcd_to_7_segment_decoder_6_p5[3], bcd_to_7_segment_decoder_6_p5[0], bcd_to_7_segment_decoder_6_p5[2], bcd_to_7_segment_decoder_6_p5[1]
  // Binary_to_BCD_converter #(.binvalue(6)) binary_to_bcd_converter_3: pin names not known; wires that end beside it: not_1_out, 1'b1, multiplexer_3_out, bcd_to_7_segment_decoder_5_p3[4], bcd_to_7_segment_decoder_5_p3[3], bcd_to_7_segment_decoder_5_p3[2]
  Comparator #(.width(6)) comparator_1 (.a(counter_1_q), .b(Hours), .eq(comparator_1_eq));  // open: gt, lt
  Comparator #(.width(6)) comparator_2 (.a(counter_2_q), .b(Mins), .eq(comparator_2_eq));  // open: gt, lt
  Comparator #(.width(6)) comparator_3 (.a(counter_3_q), .b(Secs), .eq(comparator_3_eq));  // open: gt, lt
  Blink_FSM blink_fsm_1 (
    .Reset(Set_Count), .Load(Load), .Mode(III_Cycler_FSM_1_mode), .Second_Source(blink_fsm_1_second_source),
    .Minute_Source(blink_fsm_1_minute_source), .Hour_Source(blink_fsm_1_hour_source));
  and and_1 (and_1_out, comparator_1_eq, comparator_2_eq, comparator_3_eq);
  Multiplexer #(.width(8)) multiplexer_4 (
    .in0({8{1'b0}}), .in1({1'b0, bcd_to_7_segment_decoder_1_p3}), .out(Hour_10), .sel(blink_fsm_1_hour_source));
  Multiplexer #(.width(8)) multiplexer_5 (
    .in0({8{1'b0}}), .in1({1'b1, bcd_to_7_segment_decoder_2_p5}), .out(Hour_1), .sel(blink_fsm_1_hour_source));
  Multiplexer #(.width(8)) multiplexer_6 (
    .in0({8{1'b0}}), .in1({1'b0, bcd_to_7_segment_decoder_3_p3}), .out(Min_10),
    .sel(blink_fsm_1_minute_source));
  Multiplexer #(.width(8)) multiplexer_7 (
    .in0({8{1'b0}}), .in1({1'b1, bcd_to_7_segment_decoder_4_p5}), .out(Min_1), .sel(blink_fsm_1_minute_source));
  Multiplexer #(.width(8)) multiplexer_8 (
    .in0({8{1'b0}}), .in1({1'b0, bcd_to_7_segment_decoder_5_p3}), .out(Sec_10),
    .sel(blink_fsm_1_second_source));
  Multiplexer #(.width(8)) multiplexer_9 (
    .in0({8{1'b0}}), .in1({1'b0, bcd_to_7_segment_decoder_6_p5}), .out(Sec_1), .sel(blink_fsm_1_second_source));
  or or_1 (or_1_out, Bascule_Reset, Stop_Alarm);
  Alarm_Buzzer_FSM Bascule_Alarm_FSM_1 (
    .Is_Time(and_1_out), .Alarm_Active(Activate_Alarm), .Reset(or_1_out),
    .Buzzer_Active(Bascule_Alarm_FSM_1_buzzer_active));
  and and_2 (Buzzer, Bascule_Alarm_FSM_1_buzzer_active, clock_1_out);
endmodule

module Mode_03_TimerInput_FSM (
  input  Done,
  input  StartPause,
  input  Load,
  input  CurrentStart,
  input  CurrentLoad,
  output M1,
  output G5
);

  wire and_1_out, and_2_out, and_3_out, and_4_out, and_5_out, and_6_out, not_1_out, not_2_out, not_3_out,
       not_4_out, not_5_out;

  not not_1 (not_1_out, Done);
  not not_2 (not_2_out, StartPause);
  not not_3 (not_3_out, Load);
  not not_4 (not_4_out, CurrentStart);
  not not_5 (not_5_out, CurrentLoad);
  and and_1 (and_1_out, not_2_out, Load, not_4_out);
  and and_2 (and_2_out, Load, not_4_out, CurrentLoad);
  and and_3 (and_3_out, Done, Load);
  and and_4 (and_4_out, not_1_out, StartPause, not_3_out, not_4_out);
  and and_5 (and_5_out, not_1_out, StartPause, CurrentStart, not_5_out);
  and and_6 (and_6_out, not_1_out, StartPause, not_3_out, CurrentStart);
  or or_1 (M1, and_1_out, and_2_out, and_3_out);
  or or_2 (G5, and_4_out, and_5_out, and_6_out);
endmodule

module III_Cycler_FSM (
  input  Switch,
  output [1:0] Mode
);

  wire clock_1_out, d_ff_1_q, III_Cycler_TransitionLogic_1_change;
  wire [1:0] III_Cycler_TransitionLogic_1_mode;

  Clock clock_1 (.out(clock_1_out));
  III_Cycler_TransitionLogic III_Cycler_TransitionLogic_1 (
    .current_change(d_ff_1_q), .current_mode(Mode), .Switch(Switch),
    .change(III_Cycler_TransitionLogic_1_change), .mode(III_Cycler_TransitionLogic_1_mode));
  D_Flip_Flop d_ff_1 (
    .D(III_Cycler_TransitionLogic_1_change), .clk(clock_1_out), .Q(d_ff_1_q), .preset(1'b0), .reset(1'b0));  // open: Qn
  D_Flip_Flop d_ff_2 (
    .D(III_Cycler_TransitionLogic_1_mode[0]), .clk(clock_1_out), .Q(Mode[0]), .preset(1'b0), .reset(1'b0));  // open: Qn
  D_Flip_Flop d_ff_3 (
    .D(III_Cycler_TransitionLogic_1_mode[1]), .clk(clock_1_out), .Q(Mode[1]), .preset(1'b0), .reset(1'b0));  // open: Qn
endmodule

module III_Cycler_TransitionLogic (
  input  current_change,
  input  [1:0] current_mode,
  input  Switch,
  output change,
  output [1:0] mode
);

  wire and_1_out, and_2_out, and_3_out, and_4_out, and_5_out, and_6_out, not_1_out, not_2_out, not_3_out,
       not_4_out;

  not not_1 (not_1_out, current_change);
  not not_2 (not_2_out, Switch);
  not not_3 (not_3_out, current_mode[1]);
  not not_4 (not_4_out, current_mode[0]);
  and and_1 (and_1_out, not_1_out, current_mode[1]);
  and and_2 (and_2_out, Switch, current_mode[1]);
  and and_3 (and_3_out, current_change, not_2_out, not_3_out, current_mode[0]);
  and and_4 (and_4_out, not_1_out, current_mode[0]);
  and and_5 (and_5_out, Switch, current_mode[0]);
  and and_6 (and_6_out, current_change, not_2_out, not_3_out, not_4_out);
  or or_1 (mode[1], and_1_out, and_2_out, and_3_out);
  or or_2 (mode[0], and_4_out, and_5_out, and_6_out);

  assign change = Switch;
endmodule

module IV_Cycler_FSM (
  input  Switch,
  output [1:0] Mode
);

  wire clock_1_out, d_ff_1_q, IV_Cycler_Transition_Logic_1_change;
  wire [1:0] IV_Cycler_Transition_Logic_1_mode;

  Clock clock_1 (.out(clock_1_out));
  IV_Cycler_Transition_Logic IV_Cycler_Transition_Logic_1 (
    .current_change(d_ff_1_q), .current_mode(Mode), .switch(Switch),
    .change(IV_Cycler_Transition_Logic_1_change), .mode(IV_Cycler_Transition_Logic_1_mode));
  D_Flip_Flop d_ff_1 (
    .D(IV_Cycler_Transition_Logic_1_change), .clk(clock_1_out), .Q(d_ff_1_q), .preset(1'b0), .reset(1'b0));  // open: Qn
  D_Flip_Flop d_ff_2 (
    .D(IV_Cycler_Transition_Logic_1_mode[0]), .clk(clock_1_out), .Q(Mode[0]), .preset(1'b0), .reset(1'b0));  // open: Qn
  D_Flip_Flop d_ff_3 (
    .D(IV_Cycler_Transition_Logic_1_mode[1]), .clk(clock_1_out), .Q(Mode[1]), .preset(1'b0), .reset(1'b0));  // open: Qn
endmodule

module IV_Cycler_Transition_Logic (
  input  current_change,
  input  [1:0] current_mode,
  input  switch,
  output change,
  output [1:0] mode
);

  wire and_1_out, and_2_out, and_3_out, and_4_out, and_5_out, and_6_out, and_7_out, not_1_out, not_2_out,
       not_3_out, not_4_out;

  not not_1 (not_1_out, current_change);
  not not_2 (not_2_out, switch);
  not not_3 (not_3_out, current_mode[1]);
  not not_4 (not_4_out, current_mode[0]);
  and and_1 (and_1_out, not_1_out, current_mode[1]);
  and and_2 (and_2_out, current_mode[1], not_4_out);
  and and_3 (and_3_out, switch, current_mode[1]);
  and and_4 (and_4_out, current_change, not_2_out, not_3_out, current_mode[0]);
  and and_5 (and_5_out, not_1_out, current_mode[0]);
  and and_6 (and_6_out, switch, current_mode[0]);
  and and_7 (and_7_out, current_change, not_2_out, not_4_out);
  or or_1 (mode[1], and_1_out, and_2_out, and_3_out, and_4_out);
  or or_2 (mode[0], and_5_out, and_6_out, and_7_out);

  assign change = switch;
endmodule

module Encodeur_TransitionLogic (
  input  cdir,
  input  c1,
  input  c0,
  input  i1,
  input  i0,
  output i1_out,
  output i0_out,
  output UpDown,
  output G5
);

  wire and_1_out, and_2_out, and_3_out, and_4_out, and_5_out, and_6_out, and_7_out, and_8_out, and_9_out,
       and_10_out, and_11_out, and_12_out, not_1_out, not_2_out, not_3_out, not_4_out;

  not not_1 (not_1_out, c1);
  not not_2 (not_2_out, c0);
  not not_3 (not_3_out, i1);
  not not_4 (not_4_out, i0);
  and and_1 (and_1_out, not_1_out, not_2_out, i1, not_4_out);
  and and_2 (and_2_out, not_1_out, c0, not_3_out, not_4_out);
  and and_3 (and_3_out, c1, not_2_out, i1, i0);
  and and_4 (and_4_out, c1, c0, not_3_out, i0);
  and and_5 (and_5_out, cdir, not_1_out, not_4_out);
  and and_6 (and_6_out, cdir, not_2_out, i1);
  and and_7 (and_7_out, cdir, c0, not_3_out);
  and and_8 (and_8_out, cdir, c1, i0);
  and and_9 (and_9_out, not_1_out, c0, not_3_out, not_4_out);
  and and_10 (and_10_out, not_1_out, c0, i1, i0);
  and and_11 (and_11_out, c1, not_2_out, not_3_out, not_4_out);
  and and_12 (and_12_out, c1, not_2_out, i1, i0);
  or or_1 (G5, and_9_out, and_10_out, and_11_out, and_12_out);
  or or_2 (UpDown, and_1_out, and_2_out, and_3_out, and_4_out, and_5_out, and_6_out, and_7_out, and_8_out);

  assign i0_out = i0;
  assign i1_out = i1;
endmodule

module Encodeur_FSM (
  input  CHA,
  input  CHB,
  output UpDown,
  output G5
);

  wire clock_1_out, d_ff_1_q, d_ff_2_q, Encodeur_TransitionLogic_1_i0_out, Encodeur_TransitionLogic_1_i1_out,
       Encodeur_TransitionLogic_1_updown;

  Clock clock_1 (.out(clock_1_out));
  Encodeur_TransitionLogic Encodeur_TransitionLogic_1 (
    .cdir(UpDown), .c1(d_ff_1_q), .c0(d_ff_2_q), .i1(CHA), .i0(CHB),
    .i1_out(Encodeur_TransitionLogic_1_i1_out), .i0_out(Encodeur_TransitionLogic_1_i0_out),
    .UpDown(Encodeur_TransitionLogic_1_updown), .G5(G5));
  D_Flip_Flop d_ff_1 (
    .D(Encodeur_TransitionLogic_1_i1_out), .clk(clock_1_out), .Q(d_ff_1_q), .preset(1'b0), .reset(1'b0));  // open: Qn
  D_Flip_Flop d_ff_2 (
    .D(Encodeur_TransitionLogic_1_i0_out), .clk(clock_1_out), .Q(d_ff_2_q), .preset(1'b0), .reset(1'b0));  // open: Qn
  D_Flip_Flop d_ff_3 (
    .D(Encodeur_TransitionLogic_1_updown), .clk(clock_1_out), .Q(UpDown), .preset(1'b0), .reset(1'b0));  // open: Qn
endmodule

module Display (
  input  [47:0] DisplayInput,
  output Sec_1_P,
  output Sec_1_G,
  output Sec_1_F,
  output Sec_1_E,
  output Sec_1_D,
  output Sec_1_C,
  output Sec_1_B,
  output Sec_1_A,
  output Sec_10_P,
  output Sec_10_G,
  output Sec_10_F,
  output Sec_10_E,
  output Sec_10_D,
  output Sec_10_C,
  output Sec_10_B,
  output Sec_10_A,
  output Min_1_P,
  output Min_1_G,
  output Min_1_F,
  output Min_1_E,
  output Min_1_D,
  output Min_1_C,
  output Min_1_B,
  output Min_1_A,
  output Min_10_P,
  output Min_10_G,
  output Min_10_F,
  output Min_10_E,
  output Min_10_D,
  output Min_10_C,
  output Min_10_B,
  output Min_10_A,
  output Hour_1_P,
  output Hour_1_G,
  output Hour_1_F,
  output Hour_1_E,
  output Hour_1_D,
  output Hour_1_C,
  output Hour_1_B,
  output Hour_1_A,
  output Hour_10_P,
  output Hour_10_G,
  output Hour_10_F,
  output Hour_10_E,
  output Hour_10_D,
  output Hour_10_C,
  output Hour_10_B,
  output Hour_10_A
);


  assign Hour_1_A = DisplayInput[8];
  assign Hour_1_B = DisplayInput[9];
  assign Hour_1_C = DisplayInput[10];
  assign Hour_1_D = DisplayInput[11];
  assign Hour_1_E = DisplayInput[12];
  assign Hour_1_F = DisplayInput[13];
  assign Hour_1_G = DisplayInput[14];
  assign Hour_1_P = DisplayInput[15];
  assign Hour_10_A = DisplayInput[0];
  assign Hour_10_B = DisplayInput[1];
  assign Hour_10_C = DisplayInput[2];
  assign Hour_10_D = DisplayInput[3];
  assign Hour_10_E = DisplayInput[4];
  assign Hour_10_F = DisplayInput[5];
  assign Hour_10_G = DisplayInput[6];
  assign Hour_10_P = DisplayInput[7];
  assign Min_1_A = DisplayInput[24];
  assign Min_1_B = DisplayInput[25];
  assign Min_1_C = DisplayInput[26];
  assign Min_1_D = DisplayInput[27];
  assign Min_1_E = DisplayInput[28];
  assign Min_1_F = DisplayInput[29];
  assign Min_1_G = DisplayInput[30];
  assign Min_1_P = DisplayInput[31];
  assign Min_10_A = DisplayInput[16];
  assign Min_10_B = DisplayInput[17];
  assign Min_10_C = DisplayInput[18];
  assign Min_10_D = DisplayInput[19];
  assign Min_10_E = DisplayInput[20];
  assign Min_10_F = DisplayInput[21];
  assign Min_10_G = DisplayInput[22];
  assign Min_10_P = DisplayInput[23];
  assign Sec_1_A = DisplayInput[40];
  assign Sec_1_B = DisplayInput[41];
  assign Sec_1_C = DisplayInput[42];
  assign Sec_1_D = DisplayInput[43];
  assign Sec_1_E = DisplayInput[44];
  assign Sec_1_F = DisplayInput[45];
  assign Sec_1_G = DisplayInput[46];
  assign Sec_1_P = DisplayInput[47];
  assign Sec_10_A = DisplayInput[32];
  assign Sec_10_B = DisplayInput[33];
  assign Sec_10_C = DisplayInput[34];
  assign Sec_10_D = DisplayInput[35];
  assign Sec_10_E = DisplayInput[36];
  assign Sec_10_F = DisplayInput[37];
  assign Sec_10_G = DisplayInput[38];
  assign Sec_10_P = DisplayInput[39];
endmodule

module Bascule_TransitionLogic (
  input  current_mode,
  input  current_start,
  input  start_input,
  output mode,
  output start
);

  wire and_1_out, and_2_out, and_3_out, and_4_out, not_1_out, not_2_out;

  not not_1 (not_1_out, current_start);
  not not_2 (not_2_out, start_input);
  and and_1 (and_1_out, not_2_out, current_mode);
  and and_2 (and_2_out, not_1_out, start_input);
  and and_3 (and_3_out, not_2_out, current_mode);
  and and_4 (and_4_out, current_start, start_input);
  or or_1 (mode, and_1_out, and_2_out);
  or or_2 (start, and_3_out, and_4_out);
endmodule

module Bascule_FSM (
  input  Switch,
  input  Reset,
  output Bascule_Output
);

  wire Bascule_TransitionLogic_1_mode, Bascule_TransitionLogic_1_start, clock_1_out, d_ff_1_q;

  Clock clock_1 (.out(clock_1_out));
  Bascule_TransitionLogic Bascule_TransitionLogic_1 (
    .current_mode(d_ff_1_q), .current_start(Bascule_Output), .start_input(Switch),
    .mode(Bascule_TransitionLogic_1_mode), .start(Bascule_TransitionLogic_1_start));
  D_Flip_Flop d_ff_1 (
    .D(Bascule_TransitionLogic_1_mode), .clk(clock_1_out), .Q(d_ff_1_q), .preset(1'b0), .reset(Reset));  // open: Qn
  D_Flip_Flop d_ff_2 (
    .D(Bascule_TransitionLogic_1_start), .clk(clock_1_out), .Q(Bascule_Output), .preset(1'b0), .reset(Reset));  // open: Qn
endmodule

module Init_Impulse (
  output Reset
);

  wire clock_1_out, d_ff_1_q, not_1_out, not_2_out;

  Clock clock_1 (.out(clock_1_out));
  D_Flip_Flop d_ff_1 (.D(not_1_out), .clk(clock_1_out), .Q(d_ff_1_q), .preset(1'b0), .reset(1'b0));  // open: Qn
  not not_1 (not_1_out, clock_1_out);
  D_Flip_Flop d_ff_2 (.D(not_2_out), .clk(clock_1_out), .Q(Reset), .preset(1'b0), .reset(1'b0));  // open: Qn
  not not_2 (not_2_out, d_ff_1_q);
endmodule

module Impulse (
  input  Activation,
  output Impulse_Response
);

  wire and_1_out, and_2_out, clock_1_out, d_ff_1_q, not_1_out, not_2_out;

  Clock clock_1 (.out(clock_1_out));
  and and_1 (and_1_out, Activation, not_1_out);
  not not_1 (not_1_out, clock_1_out);
  D_Flip_Flop d_ff_1 (.D(and_1_out), .clk(clock_1_out), .Q(d_ff_1_q), .preset(1'b0), .reset(1'b0));  // open: Qn
  and and_2 (and_2_out, Activation, not_2_out);
  not not_2 (not_2_out, d_ff_1_q);
  D_Flip_Flop d_ff_2 (.D(and_2_out), .clk(clock_1_out), .Q(Impulse_Response), .preset(1'b0), .reset(1'b0));  // open: Qn
endmodule

module LtR_TransitionLogic (
  input  [9:0] Current_Leds,
  output [9:0] Leds
);

  wire and_3_out, and_4_out, and_5_out, and_7_out, and_8_out, not_1_out, not_2_out;

  not not_1 (not_1_out, Current_Leds[9]);
  not not_2 (not_2_out, Current_Leds[7]);
  and and_1 (Leds[9], not_1_out, Current_Leds[8]);
  and and_2 (Leds[8], not_1_out, Current_Leds[7]);
  and and_3 (and_3_out, not_1_out, Current_Leds[6]);
  and and_4 (and_4_out, not_2_out, Current_Leds[6]);
  and and_5 (and_5_out, not_1_out, Current_Leds[8]);
  and and_6 (Leds[6], not_1_out, Current_Leds[5]);
  and and_7 (and_7_out, not_2_out, Current_Leds[4]);
  and and_8 (and_8_out, not_1_out, Current_Leds[6]);
  and and_9 (Leds[4], not_1_out, Current_Leds[3]);
  and and_10 (Leds[3], not_1_out, Current_Leds[2]);
  and and_11 (Leds[2], not_1_out, Current_Leds[1]);
  and and_12 (Leds[1], not_1_out, Current_Leds[0]);
  or or_1 (Leds[7], and_3_out, and_4_out, and_5_out);
  or or_2 (Leds[5], and_7_out, and_8_out);

  assign Leds[0] = 1'b1;
endmodule

module LtR_FSM (
  input  Counting,
  input  Reset,
  output [9:0] LEDS
);

  wire and_1_out, and_2_out, and_3_out, and_4_out, and_5_out, and_6_out, and_7_out, and_8_out, and_9_out,
       and_10_out, and_11_out, and_12_out, and_13_out, and_14_out, and_15_out, and_16_out, and_17_out,
       and_18_out, and_19_out, and_20_out, clock_1_out, not_1_out;
  wire [9:0] LtR_TransitionLogic_1_leds;

  Clock #(.highDuration(50), .lowDuration(50)) clock_1 (.out(clock_1_out));
  LtR_TransitionLogic LtR_TransitionLogic_1 (.Current_Leds(LEDS), .Leds(LtR_TransitionLogic_1_leds));
  not not_1 (not_1_out, Counting);
  D_Flip_Flop d_ff_1 (.D(and_1_out), .clk(clock_1_out), .Q(LEDS[0]), .preset(and_11_out), .reset(Reset));  // open: Qn
  and and_1 (and_1_out, LtR_TransitionLogic_1_leds[0], Counting);
  D_Flip_Flop d_ff_2 (.D(and_2_out), .clk(clock_1_out), .Q(LEDS[1]), .preset(and_12_out), .reset(Reset));  // open: Qn
  and and_2 (and_2_out, LtR_TransitionLogic_1_leds[1], Counting);
  D_Flip_Flop d_ff_3 (.D(and_3_out), .clk(clock_1_out), .Q(LEDS[2]), .preset(and_13_out), .reset(Reset));  // open: Qn
  and and_3 (and_3_out, LtR_TransitionLogic_1_leds[2], Counting);
  D_Flip_Flop d_ff_4 (.D(and_4_out), .clk(clock_1_out), .Q(LEDS[3]), .preset(and_14_out), .reset(Reset));  // open: Qn
  and and_4 (and_4_out, LtR_TransitionLogic_1_leds[3], Counting);
  D_Flip_Flop d_ff_5 (.D(and_5_out), .clk(clock_1_out), .Q(LEDS[4]), .preset(and_15_out), .reset(Reset));  // open: Qn
  and and_5 (and_5_out, LtR_TransitionLogic_1_leds[4], Counting);
  D_Flip_Flop d_ff_6 (.D(and_6_out), .clk(clock_1_out), .Q(LEDS[5]), .preset(and_16_out), .reset(Reset));  // open: Qn
  and and_6 (and_6_out, LtR_TransitionLogic_1_leds[5], Counting);
  D_Flip_Flop d_ff_7 (.D(and_7_out), .clk(clock_1_out), .Q(LEDS[6]), .preset(and_17_out), .reset(Reset));  // open: Qn
  and and_7 (and_7_out, LtR_TransitionLogic_1_leds[6], Counting);
  D_Flip_Flop d_ff_8 (.D(and_8_out), .clk(clock_1_out), .Q(LEDS[7]), .preset(and_18_out), .reset(Reset));  // open: Qn
  and and_8 (and_8_out, LtR_TransitionLogic_1_leds[7], Counting);
  D_Flip_Flop d_ff_9 (.D(and_9_out), .clk(clock_1_out), .Q(LEDS[8]), .preset(and_19_out), .reset(Reset));  // open: Qn
  and and_9 (and_9_out, LtR_TransitionLogic_1_leds[8], Counting);
  D_Flip_Flop d_ff_10 (.D(and_10_out), .clk(clock_1_out), .Q(LEDS[9]), .preset(and_20_out), .reset(Reset));  // open: Qn
  and and_10 (and_10_out, LtR_TransitionLogic_1_leds[9], Counting);
  and and_11 (and_11_out, LEDS[0], not_1_out);
  and and_12 (and_12_out, LEDS[1], not_1_out);
  and and_13 (and_13_out, LEDS[2], not_1_out);
  and and_14 (and_14_out, LEDS[3], not_1_out);
  and and_15 (and_15_out, LEDS[4], not_1_out);
  and and_16 (and_16_out, LEDS[5], not_1_out);
  and and_17 (and_17_out, LEDS[6], not_1_out);
  and and_18 (and_18_out, LEDS[7], not_1_out);
  and and_19 (and_19_out, LEDS[8], not_1_out);
  and and_20 (and_20_out, LEDS[9], not_1_out);
endmodule

module RtL_TransitionLogic (
  input  [9:0] Current_Leds,
  output [9:0] Leds
);

  or or_1 (Leds[0], Current_Leds[0], 1'b1);
  not not_1 (Leds[9], Current_Leds[1]);
  or or_2 (Leds[8], Leds[9], Current_Leds[9]);
  or or_3 (Leds[7], Leds[9], Current_Leds[8]);
  or or_4 (Leds[6], Leds[9], Current_Leds[7]);
  or or_5 (Leds[5], Leds[9], Current_Leds[6]);
  or or_6 (Leds[4], Leds[9], Current_Leds[5]);
  or or_7 (Leds[3], Leds[9], Current_Leds[4]);
  or or_8 (Leds[2], Leds[9], Current_Leds[3]);
  or or_9 (Leds[1], Leds[9], Current_Leds[2]);
endmodule

module RtL_FSM (
  input  Counting,
  input  Reset,
  output [9:0] LEDS
);

  wire and_1_out, and_2_out, and_3_out, and_4_out, and_5_out, and_6_out, and_7_out, and_8_out, and_9_out,
       and_10_out, and_11_out, and_12_out, and_13_out, and_14_out, and_15_out, and_16_out, and_17_out,
       and_18_out, and_19_out, and_20_out, clock_1_out, not_1_out;
  wire [9:0] RtL_TransitionLogic_1_leds;

  Clock #(.highDuration(50), .lowDuration(50)) clock_1 (.out(clock_1_out));
  RtL_TransitionLogic RtL_TransitionLogic_1 (.Current_Leds(LEDS), .Leds(RtL_TransitionLogic_1_leds));
  not not_1 (not_1_out, Counting);
  D_Flip_Flop d_ff_1 (.D(and_1_out), .clk(clock_1_out), .Q(LEDS[0]), .preset(and_11_out), .reset(Reset));  // open: Qn
  and and_1 (and_1_out, RtL_TransitionLogic_1_leds[0], Counting);
  D_Flip_Flop d_ff_2 (.D(and_2_out), .clk(clock_1_out), .Q(LEDS[1]), .preset(and_12_out), .reset(Reset));  // open: Qn
  and and_2 (and_2_out, RtL_TransitionLogic_1_leds[1], Counting);
  D_Flip_Flop d_ff_3 (.D(and_3_out), .clk(clock_1_out), .Q(LEDS[2]), .preset(and_13_out), .reset(Reset));  // open: Qn
  and and_3 (and_3_out, RtL_TransitionLogic_1_leds[2], Counting);
  D_Flip_Flop d_ff_4 (.D(and_4_out), .clk(clock_1_out), .Q(LEDS[3]), .preset(and_14_out), .reset(Reset));  // open: Qn
  and and_4 (and_4_out, RtL_TransitionLogic_1_leds[3], Counting);
  D_Flip_Flop d_ff_5 (.D(and_5_out), .clk(clock_1_out), .Q(LEDS[4]), .preset(and_15_out), .reset(Reset));  // open: Qn
  and and_5 (and_5_out, RtL_TransitionLogic_1_leds[4], Counting);
  D_Flip_Flop d_ff_6 (.D(and_6_out), .clk(clock_1_out), .Q(LEDS[5]), .preset(and_16_out), .reset(Reset));  // open: Qn
  and and_6 (and_6_out, RtL_TransitionLogic_1_leds[5], Counting);
  D_Flip_Flop d_ff_7 (.D(and_7_out), .clk(clock_1_out), .Q(LEDS[6]), .preset(and_17_out), .reset(Reset));  // open: Qn
  and and_7 (and_7_out, RtL_TransitionLogic_1_leds[6], Counting);
  D_Flip_Flop d_ff_8 (.D(and_8_out), .clk(clock_1_out), .Q(LEDS[7]), .preset(and_18_out), .reset(Reset));  // open: Qn
  and and_8 (and_8_out, RtL_TransitionLogic_1_leds[7], Counting);
  D_Flip_Flop d_ff_9 (.D(and_9_out), .clk(clock_1_out), .Q(LEDS[8]), .preset(and_19_out), .reset(Reset));  // open: Qn
  and and_9 (and_9_out, RtL_TransitionLogic_1_leds[8], Counting);
  D_Flip_Flop d_ff_10 (.D(and_10_out), .clk(clock_1_out), .Q(LEDS[9]), .preset(and_20_out), .reset(Reset));  // open: Qn
  and and_10 (and_10_out, RtL_TransitionLogic_1_leds[9], Counting);
  and and_11 (and_11_out, LEDS[0], not_1_out);
  and and_12 (and_12_out, LEDS[1], not_1_out);
  and and_13 (and_13_out, LEDS[2], not_1_out);
  and and_14 (and_14_out, LEDS[3], not_1_out);
  and and_15 (and_15_out, LEDS[4], not_1_out);
  and and_16 (and_16_out, LEDS[5], not_1_out);
  and and_17 (and_17_out, LEDS[6], not_1_out);
  and and_18 (and_18_out, LEDS[7], not_1_out);
  and and_19 (and_19_out, LEDS[8], not_1_out);
  and and_20 (and_20_out, LEDS[9], not_1_out);
endmodule

module Mode_TransitionLogic (
  input  [3:0] Current_Mode,
  input  Current_Changing,
  input  Message_Done,
  input  Switch_Button,
  input  Reset_General,
  output [3:0] Mode,
  output Start,
  output Reset,
  output Changing
);

  wire and_1_out, and_2_out, and_3_out, and_4_out, and_5_out, and_6_out, and_7_out, and_8_out, and_9_out,
       and_10_out, and_11_out, and_12_out, and_13_out, and_14_out, and_15_out, and_16_out, and_17_out,
       and_18_out, and_19_out, and_20_out, and_21_out, and_22_out, and_23_out, and_24_out, and_25_out,
       and_26_out, and_27_out, not_1_out, not_2_out, not_3_out, not_4_out, not_5_out, not_6_out, not_7_out,
       not_8_out;

  not not_1 (not_1_out, Reset_General);
  not not_2 (not_2_out, Current_Mode[3]);
  not not_3 (not_3_out, Current_Mode[2]);
  not not_4 (not_4_out, Current_Mode[1]);
  not not_5 (not_5_out, Current_Mode[0]);
  not not_6 (not_6_out, Current_Changing);
  not not_7 (not_7_out, Message_Done);
  not not_8 (not_8_out, Switch_Button);
  and and_1 (and_1_out, not_1_out, not_2_out, Current_Mode[2], Current_Mode[1], Current_Mode[0], Current_Changing, not_7_out);
  and and_2 (and_2_out, not_1_out, Current_Mode[3], not_3_out, not_4_out, not_5_out, not_6_out);
  and and_3 (and_3_out, not_1_out, Current_Mode[3], not_3_out, not_4_out, not_5_out, Switch_Button);
  and and_4 (and_4_out, not_1_out, not_2_out, not_3_out, Current_Mode[1], Current_Mode[0], Current_Changing, not_7_out);
  and and_5 (and_5_out, not_1_out, not_2_out, Current_Mode[2], not_4_out);
  and and_6 (and_6_out, not_1_out, not_2_out, Current_Mode[2], not_5_out);
  and and_7 (and_7_out, not_1_out, not_2_out, Current_Mode[2], not_6_out);
  and and_8 (and_8_out, not_1_out, not_2_out, Current_Mode[2], Message_Done);
  and and_9 (and_9_out, not_1_out, not_2_out, not_4_out, Current_Mode[0], Current_Changing, not_7_out);
  and and_10 (and_10_out, not_1_out, not_2_out, Current_Mode[1], not_5_out);
  and and_11 (and_11_out, not_1_out, not_2_out, Current_Mode[1], not_6_out);
  and and_12 (and_12_out, not_1_out, not_2_out, Current_Mode[1], Message_Done);
  and and_13 (and_13_out, not_1_out, not_2_out, not_3_out, not_4_out, not_5_out, Current_Changing, not_7_out);
  and and_14 (and_14_out, not_1_out, not_2_out, Current_Mode[0], not_6_out);
  and and_15 (and_15_out, not_1_out, not_2_out, Current_Mode[0], Message_Done);
  and and_16 (and_16_out, not_1_out, not_2_out, Current_Mode[1], not_5_out, Current_Changing, not_8_out);
  and and_17 (and_17_out, not_1_out, not_2_out, Current_Mode[2], not_5_out, Current_Changing, not_8_out);
  and and_18 (and_18_out, not_1_out, Current_Mode[3], not_3_out, not_4_out, not_5_out, Current_Changing, not_8_out);
  and and_19 (and_19_out, not_1_out, not_2_out, not_3_out, not_4_out, not_6_out, not_7_out);
  and and_20 (and_20_out, not_1_out, not_2_out, Current_Mode[0], not_6_out, not_7_out);
  and and_21 (and_21_out, not_1_out, not_2_out, not_3_out, not_4_out, Message_Done);
  and and_22 (and_22_out, not_1_out, not_2_out, Current_Mode[0], Message_Done);
  and and_23 (and_23_out, not_1_out, not_2_out, not_3_out, not_4_out, Message_Done);
  and and_24 (and_24_out, not_1_out, not_2_out, Current_Mode[0], Message_Done);
  and and_25 (and_25_out, not_1_out, not_2_out, Current_Mode[1], not_5_out, Switch_Button);
  and and_26 (and_26_out, not_1_out, not_2_out, Current_Mode[2], not_5_out, Switch_Button);
  and and_27 (and_27_out, not_1_out, Current_Mode[3], not_3_out, not_4_out, not_5_out, Switch_Button);
  or or_1 (Mode[3], and_1_out, and_2_out, and_3_out);
  or or_2 (Mode[2], and_4_out, and_5_out, and_6_out, and_7_out, and_8_out);
  or or_3 (Mode[1], and_9_out, and_10_out, and_11_out, and_12_out);
  or or_4 (Start, and_19_out, and_20_out);
  or or_5 (Reset, and_21_out, and_22_out);
  or or_6 (Changing, and_23_out, and_24_out, and_25_out, and_26_out, and_27_out);
  or or_7 (Mode[0], and_13_out, and_14_out, and_15_out, and_16_out, and_17_out, and_18_out);
endmodule

module Mode_FSM (
  input  Message_Done,
  input  Switch_Button,
  input  Reset_General,
  output [3:0] Mode,
  output Start,
  output Reset
);

  wire clock_1_out, d_ff_5_q, Mode_TransitionLogic_1_changing;
  wire [3:0] Mode_TransitionLogic_1_mode;

  Clock clock_1 (.out(clock_1_out));
  Mode_TransitionLogic Mode_TransitionLogic_1 (
    .Current_Mode(Mode), .Current_Changing(d_ff_5_q), .Message_Done(Message_Done),
    .Switch_Button(Switch_Button), .Reset_General(Reset_General), .Mode(Mode_TransitionLogic_1_mode),
    .Start(Start), .Reset(Reset), .Changing(Mode_TransitionLogic_1_changing));
  D_Flip_Flop d_ff_1 (
    .D(Mode_TransitionLogic_1_mode[0]), .clk(clock_1_out), .Q(Mode[0]), .preset(1'b0), .reset(1'b0));  // open: Qn
  D_Flip_Flop d_ff_2 (
    .D(Mode_TransitionLogic_1_mode[1]), .clk(clock_1_out), .Q(Mode[1]), .preset(1'b0), .reset(1'b0));  // open: Qn
  D_Flip_Flop d_ff_3 (
    .D(Mode_TransitionLogic_1_mode[2]), .clk(clock_1_out), .Q(Mode[2]), .preset(1'b0), .reset(1'b0));  // open: Qn
  D_Flip_Flop d_ff_4 (
    .D(Mode_TransitionLogic_1_mode[3]), .clk(clock_1_out), .Q(Mode[3]), .preset(1'b0), .reset(1'b0));  // open: Qn
  D_Flip_Flop d_ff_5 (
    .D(Mode_TransitionLogic_1_changing), .clk(clock_1_out), .Q(d_ff_5_q), .preset(1'b0), .reset(1'b0));  // open: Qn
endmodule

module Message_HELLO (
  input  Reset,
  input  Start,
  output [47:0] Output_To_Display,
  output Message_Done
);

  wire Fifth_of_Second_out;
  wire [3:0] Hello_Counter_q;

  Clock #(.highDuration(100), .lowDuration(100)) Fifth_of_Second (.out(Fifth_of_Second_out));
  Counter #(.max('hb), .ongoal("stay"), .trigger("falling"), .width(4)) Hello_Counter (
    .clr(Reset), .load(1'b0), .up(1'b1), .count(Start), .clk(Fifth_of_Second_out), .D(4'b0000),
    .carry(Message_Done), .Q(Hello_Counter_q));
  Multiplexer #(.enable("true"), .select(4), .width(8)) multiplexer_1 (
    .in0({8{1'b0}}), .in1({8{1'b0}}), .in2({8{1'b0}}), .in3({8{1'b0}}), .in4({8{1'b0}}), .in5({8{1'b0}}),
    .in6(8'h76), .in7(8'h79), .in8(8'h38), .in9(8'h38), .in10(8'h3f), .in11({8{1'b0}}), .in12({8{1'b0}}),
    .in13({8{1'b0}}), .in14({8{1'b0}}), .in15({8{1'b0}}), .out(Output_To_Display[7:0]),
    .sel(Hello_Counter_q), .en(1'b1));
  Multiplexer #(.enable("true"), .select(4), .width(8)) multiplexer_2 (
    .in0({8{1'b0}}), .in1({8{1'b0}}), .in2({8{1'b0}}), .in3({8{1'b0}}), .in4({8{1'b0}}), .in5(8'h76),
    .in6(8'h79), .in7(8'h38), .in8(8'h38), .in9(8'h3f), .in10({8{1'b0}}), .in11({8{1'b0}}), .in12({8{1'b0}}),
    .in13({8{1'b0}}), .in14({8{1'b0}}), .in15({8{1'b0}}), .out(Output_To_Display[15:8]),
    .sel(Hello_Counter_q), .en(1'b1));
  Multiplexer #(.enable("true"), .select(4), .width(8)) multiplexer_3 (
    .in0({8{1'b0}}), .in1({8{1'b0}}), .in2({8{1'b0}}), .in3({8{1'b0}}), .in4(8'h76), .in5(8'h79),
    .in6(8'h38), .in7(8'h38), .in8(8'h3f), .in9({8{1'b0}}), .in10({8{1'b0}}), .in11({8{1'b0}}),
    .in12({8{1'b0}}), .in13({8{1'b0}}), .in14({8{1'b0}}), .in15({8{1'b0}}), .out(Output_To_Display[23:16]),
    .sel(Hello_Counter_q), .en(1'b1));
  Multiplexer #(.enable("true"), .select(4), .width(8)) multiplexer_4 (
    .in0({8{1'b0}}), .in1({8{1'b0}}), .in2({8{1'b0}}), .in3(8'h76), .in4(8'h79), .in5(8'h38), .in6(8'h38),
    .in7(8'h3f), .in8({8{1'b0}}), .in9({8{1'b0}}), .in10({8{1'b0}}), .in11({8{1'b0}}), .in12({8{1'b0}}),
    .in13({8{1'b0}}), .in14({8{1'b0}}), .in15({8{1'b0}}), .out(Output_To_Display[31:24]),
    .sel(Hello_Counter_q), .en(1'b1));
  Multiplexer #(.enable("true"), .select(4), .width(8)) multiplexer_5 (
    .in0({8{1'b0}}), .in1({8{1'b0}}), .in2(8'h76), .in3(8'h79), .in4(8'h38), .in5(8'h38), .in6(8'h3f),
    .in7({8{1'b0}}), .in8({8{1'b0}}), .in9({8{1'b0}}), .in10({8{1'b0}}), .in11({8{1'b0}}), .in12({8{1'b0}}),
    .in13({8{1'b0}}), .in14({8{1'b0}}), .in15({8{1'b0}}), .out(Output_To_Display[39:32]),
    .sel(Hello_Counter_q), .en(1'b1));
  Multiplexer #(.enable("true"), .select(4), .width(8)) multiplexer_6 (
    .in0({8{1'b0}}), .in1(8'h76), .in2(8'h79), .in3(8'h38), .in4(8'h38), .in5(8'h3f), .in6({8{1'b0}}),
    .in7({8{1'b0}}), .in8({8{1'b0}}), .in9({8{1'b0}}), .in10({8{1'b0}}), .in11({8{1'b0}}), .in12({8{1'b0}}),
    .in13({8{1'b0}}), .in14({8{1'b0}}), .in15({8{1'b0}}), .out(Output_To_Display[47:40]),
    .sel(Hello_Counter_q), .en(1'b1));
endmodule

module Message_TIME (
  input  Reset,
  input  Start,
  output [47:0] Output_To_Display,
  output Message_Done
);

  wire Fifth_of_Second_out;
  wire [3:0] Time_Counter_q;

  Clock #(.highDuration(100), .lowDuration(100)) Fifth_of_Second (.out(Fifth_of_Second_out));
  Counter #(.max('ha), .ongoal("stay"), .trigger("falling"), .width(4)) Time_Counter (
    .clr(Reset), .load(1'b0), .up(1'b1), .count(Start), .clk(Fifth_of_Second_out), .D(4'b0000),
    .carry(Message_Done), .Q(Time_Counter_q));
  Multiplexer #(.enable("true"), .select(4), .width(8)) multiplexer_1 (
    .in0({8{1'b0}}), .in1({8{1'b0}}), .in2({8{1'b0}}), .in3({8{1'b0}}), .in4({8{1'b0}}), .in5({8{1'b0}}),
    .in6(8'h78), .in7(8'h6), .in8(8'h37), .in9(8'h79), .in10({8{1'b0}}), .in11({8{1'b0}}), .in12({8{1'b0}}),
    .in13({8{1'b0}}), .in14({8{1'b0}}), .in15({8{1'b0}}), .out(Output_To_Display[7:0]), .sel(Time_Counter_q),
    .en(1'b1));
  Multiplexer #(.enable("true"), .select(4), .width(8)) multiplexer_2 (
    .in0({8{1'b0}}), .in1({8{1'b0}}), .in2({8{1'b0}}), .in3({8{1'b0}}), .in4({8{1'b0}}), .in5(8'h78),
    .in6(8'h6), .in7(8'h37), .in8(8'h79), .in9({8{1'b0}}), .in10({8{1'b0}}), .in11({8{1'b0}}),
    .in12({8{1'b0}}), .in13({8{1'b0}}), .in14({8{1'b0}}), .in15({8{1'b0}}), .out(Output_To_Display[15:8]),
    .sel(Time_Counter_q), .en(1'b1));
  Multiplexer #(.enable("true"), .select(4), .width(8)) multiplexer_3 (
    .in0({8{1'b0}}), .in1({8{1'b0}}), .in2({8{1'b0}}), .in3({8{1'b0}}), .in4(8'h78), .in5(8'h6), .in6(8'h37),
    .in7(8'h79), .in8({8{1'b0}}), .in9({8{1'b0}}), .in10({8{1'b0}}), .in11({8{1'b0}}), .in12({8{1'b0}}),
    .in13({8{1'b0}}), .in14({8{1'b0}}), .in15({8{1'b0}}), .out(Output_To_Display[23:16]),
    .sel(Time_Counter_q), .en(1'b1));
  Multiplexer #(.enable("true"), .select(4), .width(8)) multiplexer_4 (
    .in0({8{1'b0}}), .in1({8{1'b0}}), .in2({8{1'b0}}), .in3(8'h78), .in4(8'h6), .in5(8'h37), .in6(8'h79),
    .in7({8{1'b0}}), .in8({8{1'b0}}), .in9({8{1'b0}}), .in10({8{1'b0}}), .in11({8{1'b0}}), .in12({8{1'b0}}),
    .in13({8{1'b0}}), .in14({8{1'b0}}), .in15({8{1'b0}}), .out(Output_To_Display[31:24]),
    .sel(Time_Counter_q), .en(1'b1));
  Multiplexer #(.enable("true"), .select(4), .width(8)) multiplexer_5 (
    .in0({8{1'b0}}), .in1({8{1'b0}}), .in2(8'h78), .in3(8'h6), .in4(8'h37), .in5(8'h79), .in6({8{1'b0}}),
    .in7({8{1'b0}}), .in8({8{1'b0}}), .in9({8{1'b0}}), .in10({8{1'b0}}), .in11({8{1'b0}}), .in12({8{1'b0}}),
    .in13({8{1'b0}}), .in14({8{1'b0}}), .in15({8{1'b0}}), .out(Output_To_Display[39:32]),
    .sel(Time_Counter_q), .en(1'b1));
  Multiplexer #(.enable("true"), .select(4), .width(8)) multiplexer_6 (
    .in0({8{1'b0}}), .in1(8'h78), .in2(8'h6), .in3(8'h37), .in4(8'h79), .in5({8{1'b0}}), .in6({8{1'b0}}),
    .in7({8{1'b0}}), .in8({8{1'b0}}), .in9({8{1'b0}}), .in10({8{1'b0}}), .in11({8{1'b0}}), .in12({8{1'b0}}),
    .in13({8{1'b0}}), .in14({8{1'b0}}), .in15({8{1'b0}}), .out(Output_To_Display[47:40]),
    .sel(Time_Counter_q), .en(1'b1));
endmodule

module Message_CHRONO (
  input  Reset,
  input  Start,
  output [47:0] Output_To_Display,
  output Message_Done
);

  wire Fifth_of_Second_out;
  wire [3:0] Chrono_Counter_q;

  Clock #(.highDuration(100), .lowDuration(100)) Fifth_of_Second (.out(Fifth_of_Second_out));
  Counter #(.max('hc), .ongoal("stay"), .trigger("falling"), .width(4)) Chrono_Counter (
    .clr(Reset), .load(1'b0), .up(1'b1), .count(Start), .clk(Fifth_of_Second_out), .D(4'b0000),
    .carry(Message_Done), .Q(Chrono_Counter_q));
  Multiplexer #(.enable("true"), .select(4), .width(8)) multiplexer_1 (
    .in0({8{1'b0}}), .in1({8{1'b0}}), .in2({8{1'b0}}), .in3({8{1'b0}}), .in4({8{1'b0}}), .in5({8{1'b0}}),
    .in6(8'h39), .in7(8'h76), .in8(8'h50), .in9(8'h3f), .in10(8'h54), .in11(8'h3f), .in12({8{1'b0}}),
    .in13({8{1'b0}}), .in14({8{1'b0}}), .in15({8{1'b0}}), .out(Output_To_Display[7:0]),
    .sel(Chrono_Counter_q), .en(1'b1));
  Multiplexer #(.enable("true"), .select(4), .width(8)) multiplexer_2 (
    .in0({8{1'b0}}), .in1({8{1'b0}}), .in2({8{1'b0}}), .in3({8{1'b0}}), .in4({8{1'b0}}), .in5(8'h39),
    .in6(8'h76), .in7(8'h50), .in8(8'h3f), .in9(8'h54), .in10(8'h3f), .in11({8{1'b0}}), .in12({8{1'b0}}),
    .in13({8{1'b0}}), .in14({8{1'b0}}), .in15({8{1'b0}}), .out(Output_To_Display[15:8]),
    .sel(Chrono_Counter_q), .en(1'b1));
  Multiplexer #(.enable("true"), .select(4), .width(8)) multiplexer_3 (
    .in0({8{1'b0}}), .in1({8{1'b0}}), .in2({8{1'b0}}), .in3({8{1'b0}}), .in4(8'h39), .in5(8'h76),
    .in6(8'h50), .in7(8'h3f), .in8(8'h54), .in9(8'h3f), .in10({8{1'b0}}), .in11({8{1'b0}}), .in12({8{1'b0}}),
    .in13({8{1'b0}}), .in14({8{1'b0}}), .in15({8{1'b0}}), .out(Output_To_Display[23:16]),
    .sel(Chrono_Counter_q), .en(1'b1));
  Multiplexer #(.enable("true"), .select(4), .width(8)) multiplexer_4 (
    .in0({8{1'b0}}), .in1({8{1'b0}}), .in2({8{1'b0}}), .in3(8'h39), .in4(8'h76), .in5(8'h50), .in6(8'h3f),
    .in7(8'h54), .in8(8'h3f), .in9({8{1'b0}}), .in10({8{1'b0}}), .in11({8{1'b0}}), .in12({8{1'b0}}),
    .in13({8{1'b0}}), .in14({8{1'b0}}), .in15({8{1'b0}}), .out(Output_To_Display[31:24]),
    .sel(Chrono_Counter_q), .en(1'b1));
  Multiplexer #(.enable("true"), .select(4), .width(8)) multiplexer_5 (
    .in0({8{1'b0}}), .in1({8{1'b0}}), .in2(8'h39), .in3(8'h76), .in4(8'h50), .in5(8'h3f), .in6(8'h54),
    .in7(8'h3f), .in8({8{1'b0}}), .in9({8{1'b0}}), .in10({8{1'b0}}), .in11({8{1'b0}}), .in12({8{1'b0}}),
    .in13({8{1'b0}}), .in14({8{1'b0}}), .in15({8{1'b0}}), .out(Output_To_Display[39:32]),
    .sel(Chrono_Counter_q), .en(1'b1));
  Multiplexer #(.enable("true"), .select(4), .width(8)) multiplexer_6 (
    .in0({8{1'b0}}), .in1(8'h39), .in2(8'h76), .in3(8'h50), .in4(8'h3f), .in5(8'h54), .in6(8'h3f),
    .in7({8{1'b0}}), .in8({8{1'b0}}), .in9({8{1'b0}}), .in10({8{1'b0}}), .in11({8{1'b0}}), .in12({8{1'b0}}),
    .in13({8{1'b0}}), .in14({8{1'b0}}), .in15({8{1'b0}}), .out(Output_To_Display[47:40]),
    .sel(Chrono_Counter_q), .en(1'b1));
endmodule

module Message_TIMER (
  input  Reset,
  input  Start,
  output [47:0] Output_To_Display,
  output Message_Done
);

  wire Fifth_of_Second_out;
  wire [3:0] Timer_Counter_q;

  Clock #(.highDuration(100), .lowDuration(100)) Fifth_of_Second (.out(Fifth_of_Second_out));
  Counter #(.max('hb), .ongoal("stay"), .trigger("falling"), .width(4)) Timer_Counter (
    .clr(Reset), .load(1'b0), .up(1'b1), .count(Start), .clk(Fifth_of_Second_out), .D(4'b0000),
    .carry(Message_Done), .Q(Timer_Counter_q));
  Multiplexer #(.enable("true"), .select(4), .width(8)) multiplexer_1 (
    .in0({8{1'b0}}), .in1({8{1'b0}}), .in2({8{1'b0}}), .in3({8{1'b0}}), .in4({8{1'b0}}), .in5({8{1'b0}}),
    .in6(8'h78), .in7(8'h6), .in8(8'h37), .in9(8'h79), .in10(8'h50), .in11({8{1'b0}}), .in12({8{1'b0}}),
    .in13({8{1'b0}}), .in14({8{1'b0}}), .in15({8{1'b0}}), .out(Output_To_Display[7:0]),
    .sel(Timer_Counter_q), .en(1'b1));
  Multiplexer #(.enable("true"), .select(4), .width(8)) multiplexer_2 (
    .in0({8{1'b0}}), .in1({8{1'b0}}), .in2({8{1'b0}}), .in3({8{1'b0}}), .in4({8{1'b0}}), .in5(8'h78),
    .in6(8'h6), .in7(8'h37), .in8(8'h79), .in9(8'h50), .in10({8{1'b0}}), .in11({8{1'b0}}), .in12({8{1'b0}}),
    .in13({8{1'b0}}), .in14({8{1'b0}}), .in15({8{1'b0}}), .out(Output_To_Display[15:8]),
    .sel(Timer_Counter_q), .en(1'b1));
  Multiplexer #(.enable("true"), .select(4), .width(8)) multiplexer_3 (
    .in0({8{1'b0}}), .in1({8{1'b0}}), .in2({8{1'b0}}), .in3({8{1'b0}}), .in4(8'h78), .in5(8'h6), .in6(8'h37),
    .in7(8'h79), .in8(8'h50), .in9({8{1'b0}}), .in10({8{1'b0}}), .in11({8{1'b0}}), .in12({8{1'b0}}),
    .in13({8{1'b0}}), .in14({8{1'b0}}), .in15({8{1'b0}}), .out(Output_To_Display[23:16]),
    .sel(Timer_Counter_q), .en(1'b1));
  Multiplexer #(.enable("true"), .select(4), .width(8)) multiplexer_4 (
    .in0({8{1'b0}}), .in1({8{1'b0}}), .in2({8{1'b0}}), .in3(8'h78), .in4(8'h6), .in5(8'h37), .in6(8'h79),
    .in7(8'h50), .in8({8{1'b0}}), .in9({8{1'b0}}), .in10({8{1'b0}}), .in11({8{1'b0}}), .in12({8{1'b0}}),
    .in13({8{1'b0}}), .in14({8{1'b0}}), .in15({8{1'b0}}), .out(Output_To_Display[31:24]),
    .sel(Timer_Counter_q), .en(1'b1));
  Multiplexer #(.enable("true"), .select(4), .width(8)) multiplexer_5 (
    .in0({8{1'b0}}), .in1({8{1'b0}}), .in2(8'h78), .in3(8'h6), .in4(8'h37), .in5(8'h79), .in6(8'h50),
    .in7({8{1'b0}}), .in8({8{1'b0}}), .in9({8{1'b0}}), .in10({8{1'b0}}), .in11({8{1'b0}}), .in12({8{1'b0}}),
    .in13({8{1'b0}}), .in14({8{1'b0}}), .in15({8{1'b0}}), .out(Output_To_Display[39:32]),
    .sel(Timer_Counter_q), .en(1'b1));
  Multiplexer #(.enable("true"), .select(4), .width(8)) multiplexer_6 (
    .in0({8{1'b0}}), .in1(8'h78), .in2(8'h6), .in3(8'h37), .in4(8'h79), .in5(8'h50), .in6({8{1'b0}}),
    .in7({8{1'b0}}), .in8({8{1'b0}}), .in9({8{1'b0}}), .in10({8{1'b0}}), .in11({8{1'b0}}), .in12({8{1'b0}}),
    .in13({8{1'b0}}), .in14({8{1'b0}}), .in15({8{1'b0}}), .out(Output_To_Display[47:40]),
    .sel(Timer_Counter_q), .en(1'b1));
endmodule

module Message_ALARM (
  input  Reset,
  input  Start,
  output [47:0] Output_To_Display,
  output Message_Done
);

  wire Fifth_of_Second_out;
  wire [3:0] Alarm_Counter_q;

  Clock #(.highDuration(100), .lowDuration(100)) Fifth_of_Second (.out(Fifth_of_Second_out));
  Counter #(.max('hb), .ongoal("stay"), .trigger("falling"), .width(4)) Alarm_Counter (
    .clr(Reset), .load(1'b0), .up(1'b1), .count(Start), .clk(Fifth_of_Second_out), .D(4'b0000),
    .carry(Message_Done), .Q(Alarm_Counter_q));
  Multiplexer #(.enable("true"), .select(4), .width(8)) multiplexer_1 (
    .in0({8{1'b0}}), .in1({8{1'b0}}), .in2({8{1'b0}}), .in3({8{1'b0}}), .in4({8{1'b0}}), .in5({8{1'b0}}),
    .in6(8'h77), .in7(8'h38), .in8(8'h77), .in9(8'h50), .in10(8'h37), .in11({8{1'b0}}), .in12({8{1'b0}}),
    .in13({8{1'b0}}), .in14({8{1'b0}}), .in15({8{1'b0}}), .out(Output_To_Display[7:0]),
    .sel(Alarm_Counter_q), .en(1'b1));
  Multiplexer #(.enable("true"), .select(4), .width(8)) multiplexer_2 (
    .in0({8{1'b0}}), .in1({8{1'b0}}), .in2({8{1'b0}}), .in3({8{1'b0}}), .in4({8{1'b0}}), .in5(8'h77),
    .in6(8'h38), .in7(8'h77), .in8(8'h50), .in9(8'h37), .in10({8{1'b0}}), .in11({8{1'b0}}), .in12({8{1'b0}}),
    .in13({8{1'b0}}), .in14({8{1'b0}}), .in15({8{1'b0}}), .out(Output_To_Display[15:8]),
    .sel(Alarm_Counter_q), .en(1'b1));
  Multiplexer #(.enable("true"), .select(4), .width(8)) multiplexer_3 (
    .in0({8{1'b0}}), .in1({8{1'b0}}), .in2({8{1'b0}}), .in3({8{1'b0}}), .in4(8'h77), .in5(8'h38),
    .in6(8'h77), .in7(8'h50), .in8(8'h37), .in9({8{1'b0}}), .in10({8{1'b0}}), .in11({8{1'b0}}),
    .in12({8{1'b0}}), .in13({8{1'b0}}), .in14({8{1'b0}}), .in15({8{1'b0}}), .out(Output_To_Display[23:16]),
    .sel(Alarm_Counter_q), .en(1'b1));
  Multiplexer #(.enable("true"), .select(4), .width(8)) multiplexer_4 (
    .in0({8{1'b0}}), .in1({8{1'b0}}), .in2({8{1'b0}}), .in3(8'h77), .in4(8'h38), .in5(8'h77), .in6(8'h50),
    .in7(8'h37), .in8({8{1'b0}}), .in9({8{1'b0}}), .in10({8{1'b0}}), .in11({8{1'b0}}), .in12({8{1'b0}}),
    .in13({8{1'b0}}), .in14({8{1'b0}}), .in15({8{1'b0}}), .out(Output_To_Display[31:24]),
    .sel(Alarm_Counter_q), .en(1'b1));
  Multiplexer #(.enable("true"), .select(4), .width(8)) multiplexer_5 (
    .in0({8{1'b0}}), .in1({8{1'b0}}), .in2(8'h77), .in3(8'h38), .in4(8'h77), .in5(8'h50), .in6(8'h37),
    .in7({8{1'b0}}), .in8({8{1'b0}}), .in9({8{1'b0}}), .in10({8{1'b0}}), .in11({8{1'b0}}), .in12({8{1'b0}}),
    .in13({8{1'b0}}), .in14({8{1'b0}}), .in15({8{1'b0}}), .out(Output_To_Display[39:32]),
    .sel(Alarm_Counter_q), .en(1'b1));
  Multiplexer #(.enable("true"), .select(4), .width(8)) multiplexer_6 (
    .in0({8{1'b0}}), .in1(8'h77), .in2(8'h38), .in3(8'h77), .in4(8'h50), .in5(8'h37), .in6({8{1'b0}}),
    .in7({8{1'b0}}), .in8({8{1'b0}}), .in9({8{1'b0}}), .in10({8{1'b0}}), .in11({8{1'b0}}), .in12({8{1'b0}}),
    .in13({8{1'b0}}), .in14({8{1'b0}}), .in15({8{1'b0}}), .out(Output_To_Display[47:40]),
    .sel(Alarm_Counter_q), .en(1'b1));
endmodule

module Alarm_Buzzer_TransitionLogic (
  input  Alarm_Active,
  input  current_Buzzer,
  input  current_changing,
  input  Is_Time,
  output changing,
  output Buzzer
);

  wire and_1_out, and_2_out, and_3_out, and_4_out, and_5_out, not_1_out;

  not not_1 (not_1_out, current_Buzzer);
  and and_1 (and_1_out, Alarm_Active, not_1_out, Is_Time);
  and and_2 (and_2_out, Alarm_Active, current_changing, Is_Time);
  and and_3 (and_3_out, Alarm_Active, Is_Time);
  and and_4 (and_4_out, Alarm_Active, current_changing);
  and and_5 (and_5_out, Alarm_Active, current_Buzzer);
  or or_1 (changing, and_1_out, and_2_out);
  or or_2 (Buzzer, and_3_out, and_4_out, and_5_out);
endmodule

module Alarm_Buzzer_FSM (
  input  Is_Time,
  input  Alarm_Active,
  input  Reset,
  output Buzzer_Active
);

  wire Bascule_01_q, Bascule_Alarm_TransitionLogic_1_buzzer, Bascule_Alarm_TransitionLogic_1_changing,
       clock_1_out;

  Clock clock_1 (.out(clock_1_out));
  Alarm_Buzzer_TransitionLogic Bascule_Alarm_TransitionLogic_1 (
    .Alarm_Active(Alarm_Active), .current_Buzzer(Buzzer_Active), .current_changing(Bascule_01_q),
    .Is_Time(Is_Time), .changing(Bascule_Alarm_TransitionLogic_1_changing),
    .Buzzer(Bascule_Alarm_TransitionLogic_1_buzzer));
  D_Flip_Flop Bascule_01 (
    .D(Bascule_Alarm_TransitionLogic_1_changing), .clk(clock_1_out), .Q(Bascule_01_q), .preset(1'b0),
    .reset(Reset));  // open: Qn
  D_Flip_Flop Bascule_02 (
    .D(Bascule_Alarm_TransitionLogic_1_buzzer), .clk(clock_1_out), .Q(Buzzer_Active), .preset(1'b0),
    .reset(Reset));  // open: Qn
endmodule

module Timer_Buzzer_Transition_Logic (
  input  stop,
  input  Is_Time,
  input  is_active,
  input  start,
  output Buzzer,
  output active
);

  wire and_1_out, and_2_out, and_3_out, and_4_out, and_5_out, not_1_out, not_2_out, not_3_out;

  not not_1 (not_1_out, stop);
  not not_2 (not_2_out, Is_Time);
  not not_3 (not_3_out, is_active);
  and and_1 (and_1_out, not_1_out, Is_Time, start);
  and and_2 (and_2_out, not_1_out, Is_Time, is_active);
  and and_3 (and_3_out, not_3_out, start);
  and and_4 (and_4_out, not_1_out, is_active);
  and and_5 (and_5_out, not_2_out, is_active);
  or or_1 (Buzzer, and_1_out, and_2_out);
  or or_2 (active, and_3_out, and_4_out, and_5_out);
endmodule

module Timer_Buzzer_FSM (
  input  Stop,
  input  Is_Time,
  input  Start,
  input  Reset_General,
  output Buzzer
);

  wire Bascule_D_2_q, KHz_Clock_out, Time_Bascule_TransitionLogic_1_active,
       Time_Bascule_TransitionLogic_1_buzzer;

  Clock KHz_Clock (.out(KHz_Clock_out));
  D_Flip_Flop Bascule_D_1 (
    .D(Time_Bascule_TransitionLogic_1_buzzer), .clk(KHz_Clock_out), .Q(Buzzer), .preset(1'b0),
    .reset(Reset_General));  // open: Qn
  Timer_Buzzer_Transition_Logic Time_Bascule_TransitionLogic_1 (
    .stop(Stop), .Is_Time(Is_Time), .is_active(Bascule_D_2_q), .start(Start),
    .Buzzer(Time_Bascule_TransitionLogic_1_buzzer), .active(Time_Bascule_TransitionLogic_1_active));
  D_Flip_Flop Bascule_D_2 (
    .D(Time_Bascule_TransitionLogic_1_active), .clk(KHz_Clock_out), .Q(Bascule_D_2_q), .preset(1'b0),
    .reset(Reset_General));  // open: Qn
endmodule

module Blink_TransitionLogic (
  input  current_clock,
  input  reset,
  input  load,
  input  [1:0] mode,
  output Second_Source,
  output Minute_Source,
  output Hour_Source,
  output clock
);

  wire and_1_out, and_2_out, not_1_out, not_2_out, not_3_out, not_4_out, not_5_out;

  not not_1 (not_1_out, reset);
  not not_2 (not_2_out, load);
  not not_3 (not_3_out, mode[1]);
  not not_4 (not_4_out, mode[0]);
  not not_5 (not_5_out, current_clock);
  or or_1 (Second_Source, not_2_out, not_5_out, mode[0], mode[1], reset);
  or or_2 (Minute_Source, not_2_out, not_4_out, not_5_out, reset);
  or or_3 (Hour_Source, not_2_out, not_3_out, not_5_out, mode[0], reset);
  and and_1 (and_1_out, not_1_out, not_2_out);
  and and_2 (and_2_out, not_1_out, not_5_out);
  or or_4 (clock, and_1_out, and_2_out);
endmodule

module Blink_FSM (
  input  Reset,
  input  Load,
  input  [1:0] Mode,
  output Second_Source,
  output Minute_Source,
  output Hour_Source
);

  wire clock_1_out, d_ff_1_q, Transition_Logic_Block_clock;

  Clock #(.highDuration(125), .lowDuration(125)) clock_1 (.out(clock_1_out));
  Blink_TransitionLogic Transition_Logic_Block (
    .current_clock(d_ff_1_q), .reset(Reset), .load(Load), .mode(Mode), .Second_Source(Second_Source),
    .Minute_Source(Minute_Source), .Hour_Source(Hour_Source), .clock(Transition_Logic_Block_clock));
  D_Flip_Flop d_ff_1 (
    .D(Transition_Logic_Block_clock), .clk(clock_1_out), .Q(d_ff_1_q), .preset(1'b0), .reset(1'b0));  // open: Qn
endmodule

module REVEIL_MATIN (
  input  in_1
);

  wire button_1_out, button_2_out, button_3_out, button_4_out, button_5_out, button_6_out, button_7_out,
       button_8_out, display_1_hour_1_a, display_1_hour_1_b, display_1_hour_1_c, display_1_hour_1_d,
       display_1_hour_1_e, display_1_hour_1_f, display_1_hour_1_g, display_1_hour_1_p, display_1_hour_10_a,
       display_1_hour_10_b, display_1_hour_10_c, display_1_hour_10_d, display_1_hour_10_e,
       display_1_hour_10_f, display_1_hour_10_g, display_1_hour_10_p, display_1_min_1_a, display_1_min_1_b,
       display_1_min_1_c, display_1_min_1_d, display_1_min_1_e, display_1_min_1_f, display_1_min_1_g,
       display_1_min_1_p, display_1_min_10_a, display_1_min_10_b, display_1_min_10_c, display_1_min_10_d,
       display_1_min_10_e, display_1_min_10_f, display_1_min_10_g, display_1_min_10_p, display_1_sec_1_a,
       display_1_sec_1_b, display_1_sec_1_c, display_1_sec_1_d, display_1_sec_1_e, display_1_sec_1_f,
       display_1_sec_1_g, display_1_sec_1_p, display_1_sec_10_a, display_1_sec_10_b, display_1_sec_10_c,
       display_1_sec_10_d, display_1_sec_10_e, display_1_sec_10_f, display_1_sec_10_g, display_1_sec_10_p,
       main_1_buzzer_output, main_1_led_0, main_1_led_1, main_1_led_2, main_1_led_3, main_1_led_4,
       main_1_led_5, main_1_led_6, main_1_led_7, main_1_led_8, main_1_led_9;
  wire [47:0] main_1_display;

  _7_Segment_Display u_7_segment_display_1 (
    .g(display_1_hour_10_g), .f(display_1_hour_10_f), .a(display_1_hour_10_a), .b(display_1_hour_10_b),
    .e(display_1_hour_10_e), .d(display_1_hour_10_d), .c(display_1_hour_10_c), .dp(display_1_hour_10_p));
  Display display_1 (
    .Hour_1_F(display_1_hour_1_f), .Hour_1_E(display_1_hour_1_e), .Hour_1_D(display_1_hour_1_d),
    .Hour_1_C(display_1_hour_1_c), .Hour_1_B(display_1_hour_1_b), .Hour_1_A(display_1_hour_1_a),
    .Hour_10_P(display_1_hour_10_p), .Hour_10_G(display_1_hour_10_g), .Hour_10_F(display_1_hour_10_f),
    .Hour_10_E(display_1_hour_10_e), .Hour_10_D(display_1_hour_10_d), .Hour_10_C(display_1_hour_10_c),
    .Hour_10_B(display_1_hour_10_b), .Hour_10_A(display_1_hour_10_a), .Sec_1_P(display_1_sec_1_p),
    .Sec_1_G(display_1_sec_1_g), .Sec_1_F(display_1_sec_1_f), .Sec_1_E(display_1_sec_1_e),
    .Sec_1_D(display_1_sec_1_d), .Sec_1_C(display_1_sec_1_c), .Sec_1_B(display_1_sec_1_b),
    .Sec_1_A(display_1_sec_1_a), .Sec_10_P(display_1_sec_10_p), .Sec_10_G(display_1_sec_10_g),
    .Sec_10_F(display_1_sec_10_f), .Sec_10_E(display_1_sec_10_e), .Sec_10_D(display_1_sec_10_d),
    .Sec_10_C(display_1_sec_10_c), .Sec_10_B(display_1_sec_10_b), .Sec_10_A(display_1_sec_10_a),
    .Min_1_P(display_1_min_1_p), .Min_1_G(display_1_min_1_g), .Min_1_F(display_1_min_1_f),
    .Min_1_E(display_1_min_1_e), .Min_1_D(display_1_min_1_d), .Min_1_C(display_1_min_1_c),
    .Min_1_B(display_1_min_1_b), .Min_1_A(display_1_min_1_a), .Min_10_P(display_1_min_10_p),
    .Min_10_G(display_1_min_10_g), .Min_10_F(display_1_min_10_f), .Min_10_E(display_1_min_10_e),
    .Min_10_D(display_1_min_10_d), .Min_10_C(display_1_min_10_c), .Min_10_B(display_1_min_10_b),
    .Min_10_A(display_1_min_10_a), .Hour_1_P(display_1_hour_1_p), .Hour_1_G(display_1_hour_1_g),
    .DisplayInput(main_1_display));
  LED led_1 (.in(main_1_led_0));
  LED led_2 (.in(main_1_led_1));
  Button button_1 (.out(button_1_out));
  _7_Segment_Display u_7_segment_display_2 (
    .g(display_1_min_10_g), .f(display_1_min_10_f), .a(display_1_min_10_a), .b(display_1_min_10_b),
    .e(display_1_min_10_e), .d(display_1_min_10_d), .c(display_1_min_10_c), .dp(display_1_min_10_p));
  _7_Segment_Display u_7_segment_display_3 (
    .g(display_1_hour_1_g), .f(display_1_hour_1_f), .a(display_1_hour_1_a), .b(display_1_hour_1_b),
    .e(display_1_hour_1_e), .d(display_1_hour_1_d), .c(display_1_hour_1_c), .dp(display_1_hour_1_p));
  LED led_3 (.in(main_1_led_3));
  LED led_4 (.in(main_1_led_4));
  LED led_5 (.in(main_1_led_5));
  LED led_6 (.in(main_1_led_2));
  Button button_2 (.out(button_2_out));
  _7_Segment_Display u_7_segment_display_4 (
    .g(display_1_min_1_g), .f(display_1_min_1_f), .a(display_1_min_1_a), .b(display_1_min_1_b),
    .e(display_1_min_1_e), .d(display_1_min_1_d), .c(display_1_min_1_c), .dp(display_1_min_1_p));
  LED led_7 (.in(main_1_led_6));
  LED led_8 (.in(main_1_led_7));
  LED led_9 (.in(main_1_led_8));
  LED led_10 (.in(main_1_led_9));
  Button button_3 (.out(button_3_out));
  Button button_4 (.out(button_4_out));
  Button button_5 (.out(button_5_out));
  _7_Segment_Display u_7_segment_display_5 (
    .g(display_1_sec_10_g), .f(display_1_sec_10_f), .a(display_1_sec_10_a), .b(display_1_sec_10_b),
    .e(display_1_sec_10_e), .d(display_1_sec_10_d), .c(display_1_sec_10_c), .dp(display_1_sec_10_p));
  _7_Segment_Display u_7_segment_display_6 (
    .g(display_1_sec_1_g), .f(display_1_sec_1_f), .a(display_1_sec_1_a), .b(display_1_sec_1_b),
    .e(display_1_sec_1_e), .d(display_1_sec_1_d), .c(display_1_sec_1_c), .dp(display_1_sec_1_p));
  LED led_11 (.in(main_1_buzzer_output));
  Button button_6 (.out(button_6_out));
  Button button_7 (.out(button_7_out));
  main main_1 (
    .Display(main_1_display), .LED_0(main_1_led_0), .Buzzer_Output(main_1_buzzer_output),
    .LED_1(main_1_led_1), .LED_2(main_1_led_2), .LED_3(main_1_led_3), .LED_4(main_1_led_4),
    .LED_5(main_1_led_5), .LED_6(main_1_led_6), .LED_7(main_1_led_7), .LED_8(main_1_led_8),
    .LED_9(main_1_led_9), .Start(button_6_out), .Switch_Mode(button_7_out), .Stop_Alarm(button_2_out),
    .Actiavte_Alarm(button_1_out), .Set(in_1), .CHA(button_4_out), .CHB(button_5_out), .CHC(button_3_out),
    .Reset(button_8_out));
  Button button_8 (.out(button_8_out));
endmodule
